// Logisim project Guia_0401.circ as structural Verilog: 5 circuits, main circuit Guia_0401a
module Guia_0401a (
  input  X,
  input  Y,
  input  Z,
  output S
);

  wire not_1_out, not_2_out, not_3_out, or_1_out;

  not not_1 (not_1_out, X);
  not not_2 (not_2_out, Y);
  or or_1 (or_1_out, not_2_out, Z);
  not not_3 (not_3_out, or_1_out);
  and and_1 (S, not_1_out, not_3_out);
endmodule

module Guia_0401b (
  input  X,
  input  Y,
  input  Z,
  output S
);

  wire not_1_out, not_2_out, not_3_out, or_1_out;

  not not_1 (not_1_out, X);
  not not_2 (not_2_out, Y);
  or or_1 (or_1_out, not_1_out, not_2_out);
  not not_3 (not_3_out, or_1_out);
  and and_1 (S, not_3_out, Z);
endmodule

module Guia_0401c (
  input  X,
  input  Y,
  input  Z,
  output S
);

  wire and_1_out, not_1_out, not_2_out, not_3_out;

  not not_1 (not_1_out, Y);
  not not_2 (not_2_out, Z);
  and and_1 (and_1_out, X, not_1_out);
  not not_3 (not_3_out, and_1_out);
  and and_2 (S, not_3_out, not_2_out);
endmodule

module Guia_0401d (
  input  X,
  input  Y,
  input  Z,
  output S
);

  wire and_1_out, not_1_out, not_2_out;

  not not_1 (not_1_out, X);
  and and_1 (and_1_out, not_1_out, Y);
  not not_2 (not_2_out, and_1_out);
  and and_2 (S, not_2_out, Z);
endmodule

module Guia_0401e (
  input  X,
  input  Y,
  input  Z,
  output S
);

  wire not_1_out, not_2_out, not_3_out, or_1_out, or_2_out;

  not not_1 (not_1_out, X);
  not not_2 (not_2_out, Y);
  or or_1 (or_1_out, not_1_out, Y);
  or or_2 (or_2_out, not_2_out, Z);
  not not_3 (not_3_out, or_2_out);
  and and_1 (S, or_1_out, not_3_out);
endmodule
