// Logisim project Guia_0502.circ as structural Verilog: 1 circuit, main circuit main
module main (
  input  a,
  input  b,
  output out_3,
  output out_4
);

  wire nand_1_out, not_1_out;

  not not_1 (not_1_out, b);
  nand nand_1 (nand_1_out, a, a);
  or or_1 (out_3, a, not_1_out);
  nand nand_2 (out_4, nand_1_out, b);
endmodule
