// Logisim project Guia_0503.circ as structural Verilog: 1 circuit, main circuit main
module main (
  input  a,
  input  b,
  output out_3,
  output out_4
);

  wire nor_1_out, not_1_out;

  not not_1 (not_1_out, a);
  nor nor_1 (nor_1_out, a, a);
  nor nor_2 (out_3, not_1_out, b);
  nor nor_3 (out_4, nor_1_out, b);
endmodule
