// Logisim project Guia_0504.circ as structural Verilog: 1 circuit, main circuit main
module main (
  input  a,
  input  b,
  output out_3,
  output out_4
);

  wire nand_1_out, not_1_out;

  not not_1 (not_1_out, a);
  nand nand_1 (nand_1_out, a, a);
  nand nand_2 (out_3, not_1_out, b);
  nand nand_3 (out_4, nand_1_out, b);
endmodule
