// Logisim project Guia_0506.circ as structural Verilog: 1 circuit, main circuit main
module main (
  input  a,
  input  b,
  output out_3,
  output out_4
);

  wire nand_1_out, nand_2_out, nand_3_out, nand_5_out;

  xor xor_1 (out_3, a, b);
  nand nand_1 (nand_1_out, b, b);
  nand nand_2 (nand_2_out, a, a);
  nand nand_3 (nand_3_out, a, nand_1_out);
  nand nand_4 (out_4, nand_3_out, nand_5_out);
  nand nand_5 (nand_5_out, nand_2_out, b);
endmodule
