// Logisim project Guia_0507.circ as structural Verilog: 1 circuit, main circuit main
module main (
  input  a,
  input  b,
  output out_3,
  output out_4
);

  wire nor_1_out, nor_2_out, nor_3_out, nor_4_out, nor_5_out, not_1_out, not_2_out;

  not not_1 (not_1_out, a);
  not not_2 (not_2_out, b);
  nor nor_1 (nor_1_out, a, a);
  nor nor_2 (nor_2_out, b, b);
  xor xor_1 (out_3, not_1_out, not_2_out);
  nor nor_3 (nor_3_out, nor_1_out, b);
  nor nor_4 (nor_4_out, nor_3_out, nor_5_out);
  nor nor_5 (nor_5_out, a, nor_2_out);
  nor nor_6 (out_4, nor_4_out, nor_4_out);
endmodule
