// Logisim project Guia_0508.circ as structural Verilog: 1 circuit, main circuit main
module main (
  input  a,
  input  b,
  output out_3,
  output out_4
);

  wire nand_1_out, not_1_out, not_2_out;

  not not_1 (not_1_out, a);
  not not_2 (not_2_out, b);
  nand nand_1 (nand_1_out, a, b);
  nor nor_1 (out_3, not_1_out, not_2_out);
  nand nand_2 (out_4, nand_1_out, nand_1_out);
endmodule
