// Logisim project Guia_0606.circ as structural Verilog: 1 circuit, main circuit main
module main (
  input  X,
  input  Y,
  input  W,
  input  Z,
  output S,
  output T
);

  wire and_1_out, and_2_out, and_3_out, not_1_out, not_2_out, not_3_out, not_4_out, not_5_out, not_6_out,
       not_7_out, not_8_out, not_9_out, not_10_out, or_1_out, or_2_out, or_3_out;

  not not_1 (not_1_out, Y);
  not not_2 (not_2_out, X);
  not not_3 (not_3_out, W);
  and and_1 (and_1_out, Z, W, Y);
  not not_4 (not_4_out, Y);
  or or_1 (or_1_out, not_1_out, W, not_2_out);
  and and_2 (and_2_out, Y, not_3_out, X);
  not not_5 (not_5_out, X);
  not not_6 (not_6_out, W);
  not not_7 (not_7_out, or_1_out);
  not not_8 (not_8_out, and_2_out);
  or or_2 (or_2_out, and_1_out, not_5_out);
  not not_9 (not_9_out, Z);
  and and_3 (and_3_out, not_7_out, not_8_out);
  not not_10 (not_10_out, or_2_out);
  or or_3 (or_3_out, not_4_out, not_6_out, not_9_out);
  or or_4 (S, and_3_out, not_10_out);
  and and_4 (T, X, or_3_out);
endmodule
