// Logisim project Guia_0605.circ as structural Verilog: 1 circuit, main circuit main
module main (
  input  X,
  input  Y,
  input  Z,
  output S,
  output T
);

  wire and_1_out, and_2_out, and_4_out, not_1_out, not_2_out, not_3_out, not_4_out, not_5_out, not_6_out,
       not_7_out, not_8_out, or_1_out, or_2_out, or_3_out;

  not not_1 (not_1_out, Y);
  or or_1 (or_1_out, not_1_out, not_2_out);
  not not_2 (not_2_out, X);
  and and_1 (and_1_out, Y, X);
  and and_2 (and_2_out, Z, Y);
  not not_3 (not_3_out, X);
  not not_4 (not_4_out, Z);
  or or_2 (or_2_out, not_4_out, not_5_out);
  not not_5 (not_5_out, Y);
  not not_6 (not_6_out, or_1_out);
  not not_7 (not_7_out, and_1_out);
  or or_3 (or_3_out, and_2_out, not_3_out);
  and and_3 (T, X, or_2_out);
  and and_4 (and_4_out, not_6_out, not_7_out);
  not not_8 (not_8_out, or_3_out);
  or or_4 (S, and_4_out, not_8_out);
endmodule
