// Logisim project Guia_0701.circ as structural Verilog: 1 circuit, main circuit main
module main (
  input  x,
  input  y,
  input  a,
  output s,
  output t,
  output u
);

  wire and_2_out, and_3_out, nand_2_out, not_1_out;

  not not_1 (not_1_out, a);
  and and_1 (s, y, x);
  nand nand_1 (t, y, x);
  and and_2 (and_2_out, y, x, not_1_out);
  nand nand_2 (nand_2_out, y, x);
  and and_3 (and_3_out, nand_2_out, a);
  or or_1 (u, and_2_out, and_3_out);
endmodule
