// Logisim project Guia_0702.circ as structural Verilog: 1 circuit, main circuit main
module main (
  input  x,
  input  y,
  input  a,
  output s
);

  wire and_1_out, and_2_out, nor_1_out, not_1_out, or_1_out;

  or or_1 (or_1_out, y, x);
  not not_1 (not_1_out, a);
  nor nor_1 (nor_1_out, y, x);
  and and_1 (and_1_out, or_1_out, not_1_out);
  and and_2 (and_2_out, nor_1_out, a);
  or or_2 (s, and_1_out, and_2_out);
endmodule
