// Logisim project Guia_0704.circ as structural Verilog: 1 circuit, main circuit main
module main (
  input  x,
  input  y,
  input  a,
  input  b,
  output s
);

  wire and_1_out, and_2_out, and_3_out, and_4_out, nor_1_out, not_1_out, not_2_out, or_1_out, xnor_1_out,
       xor_1_out;

  not not_1 (not_1_out, a);
  not not_2 (not_2_out, b);
  nor nor_1 (nor_1_out, x, y);
  or or_1 (or_1_out, x, y);
  xor xor_1 (xor_1_out, x, y);
  xnor xnor_1 (xnor_1_out, x, y);
  and and_1 (and_1_out, nor_1_out, not_2_out, not_1_out);
  and and_2 (and_2_out, or_1_out, b, not_1_out);
  and and_3 (and_3_out, xor_1_out, not_2_out, a);
  and and_4 (and_4_out, xnor_1_out, b, a);
  or or_2 (s, and_1_out, and_2_out, and_3_out, and_4_out);
endmodule
