// Logisim project Guia_0703.circ as structural Verilog: 1 circuit, main circuit main
module main (
  input  x,
  input  y,
  input  a,
  input  b,
  output s
);

  wire and_1_out, and_2_out, and_3_out, and_4_out, and_5_out, and_6_out, and_7_out, and_8_out, nand_1_out,
       nor_1_out, not_1_out, not_2_out, or_1_out;

  not not_1 (not_1_out, a);
  and and_1 (and_1_out, x, y, not_1_out);
  nand nand_1 (nand_1_out, x, y);
  or or_1 (or_1_out, x, y);
  nor nor_1 (nor_1_out, x, y);
  not not_2 (not_2_out, b);
  and and_2 (and_2_out, nand_1_out, a);
  and and_3 (and_3_out, or_1_out, not_1_out);
  and and_4 (and_4_out, nor_1_out, a);
  and and_5 (and_5_out, and_1_out, not_2_out);
  and and_6 (and_6_out, and_2_out, not_2_out);
  and and_7 (and_7_out, and_3_out, b);
  and and_8 (and_8_out, and_4_out, b);
  or or_2 (s, and_5_out, and_6_out, and_7_out, and_8_out);
endmodule
