// Logisim project Guia_0705.circ as structural Verilog: 1 circuit, main circuit main
module main (
  input  x,
  input  y,
  input  a,
  input  b,
  input  c,
  output s
);

  wire and_1_out, and_2_out, and_3_out, and_4_out, and_5_out, and_6_out, and_7_out, and_8_out, nand_1_out,
       nor_1_out, not_1_out, not_2_out, not_3_out, not_4_out, not_5_out, or_1_out, xnor_1_out, xor_1_out;

  not not_1 (not_1_out, a);
  not not_2 (not_2_out, c);
  not not_3 (not_3_out, b);
  not not_4 (not_4_out, x);
  not not_5 (not_5_out, y);
  and and_1 (and_1_out, not_4_out, not_1_out, not_3_out, not_2_out);
  and and_2 (and_2_out, not_5_out, not_1_out, not_3_out, c);
  and and_3 (and_3_out, x, y, not_1_out, b, not_2_out);
  nand nand_1 (nand_1_out, x, y);
  or or_1 (or_1_out, x, y);
  nor nor_1 (nor_1_out, x, y);
  xor xor_1 (xor_1_out, x, y);
  xnor xnor_1 (xnor_1_out, x, y);
  and and_4 (and_4_out, nand_1_out, not_1_out, b, c);
  and and_5 (and_5_out, or_1_out, a, not_3_out, not_2_out);
  and and_6 (and_6_out, nor_1_out, a, not_3_out, c);
  and and_7 (and_7_out, xor_1_out, a, b, not_2_out);
  and and_8 (and_8_out, xnor_1_out, a, b, c);
  or or_2 (s, and_1_out, and_2_out, and_3_out, and_4_out, and_5_out, and_6_out, and_7_out, and_8_out);
endmodule
