// Logisim project G08.circ as structural Verilog: 5 circuits, main circuit 01
module _01 (
  input  b3,
  input  b2,
  input  b1,
  input  b0,
  input  a3,
  input  a2,
  input  a1,
  input  a0,
  output c3,
  output c2,
  output c1,
  output c0
);

  wire and_1_out, and_2_out, and_3_out, and_4_out, and_5_out, and_6_out, or_1_out, or_2_out, or_3_out,
       xor_2_out, xor_3_out, xor_6_out, xor_8_out;

  xor xor_1 (c3, xor_2_out, or_1_out);
  xor xor_2 (xor_2_out, b3, a3);
  and and_1 (and_1_out, b2, a2);
  or or_1 (or_1_out, and_1_out, and_2_out);
  and and_2 (and_2_out, or_2_out, xor_3_out);
  xor xor_3 (xor_3_out, b2, a2);
  xor xor_4 (c2, xor_3_out, or_2_out);
  or or_2 (or_2_out, and_3_out, and_4_out);
  xor xor_5 (c1, xor_6_out, or_3_out);
  and and_3 (and_3_out, b1, a1);
  and and_4 (and_4_out, or_3_out, xor_6_out);
  xor xor_6 (xor_6_out, b1, a1);
  or or_3 (or_3_out, and_5_out, and_6_out);
  xor xor_7 (c0, xor_8_out, 1'b0);
  and and_5 (and_5_out, b0, a0);
  and and_6 (and_6_out, 1'b0, xor_8_out);
  xor xor_8 (xor_8_out, b0, a0);
endmodule

module _03 (
  input  a4,
  input  a3,
  input  a2,
  input  a1,
  input  a0,
  input  b4,
  input  b3,
  input  b2,
  input  b1,
  input  b0,
  output s
);

  wire xnor_1_out, xnor_2_out, xnor_3_out, xnor_4_out, xnor_5_out;

  xnor xnor_1 (xnor_1_out, b4, a4);
  xnor xnor_2 (xnor_2_out, b3, a3);
  xnor xnor_3 (xnor_3_out, b1, a1);
  xnor xnor_4 (xnor_4_out, b2, a2);
  and and_1 (s, xnor_1_out, xnor_2_out, xnor_4_out, xnor_3_out, xnor_5_out);
  xnor xnor_5 (xnor_5_out, b0, a0);
endmodule

module _04 (
  input  a4,
  input  a3,
  input  a2,
  input  a1,
  input  a0,
  input  b4,
  input  b3,
  input  b2,
  input  b1,
  input  b0,
  output s
);

  wire xor_1_out, xor_2_out, xor_3_out, xor_4_out, xor_5_out;

  xor xor_1 (xor_1_out, b3, a3);
  xor xor_2 (xor_2_out, b4, a4);
  xor xor_3 (xor_3_out, b1, a1);
  xor xor_4 (xor_4_out, b2, a2);
  or or_1 (s, xor_2_out, xor_1_out, xor_4_out, xor_3_out, xor_5_out);
  xor xor_5 (xor_5_out, b0, a0);
endmodule

module _05 (
  input  a5,
  input  a4,
  input  a3,
  input  a2,
  input  a1,
  input  a0,
  output s6,
  output s5,
  output s4,
  output s3,
  output s2,
  output s1,
  output s0
);

  wire and_1_out, and_2_out, and_3_out, and_4_out, and_5_out, not_1_out, not_2_out, not_3_out, not_4_out,
       not_5_out, not_6_out;

  xor xor_1 (s5, not_1_out, and_1_out);
  not not_1 (not_1_out, a5);
  and and_1 (and_1_out, and_2_out, not_2_out);
  xor xor_2 (s4, not_2_out, and_2_out);
  not not_2 (not_2_out, a4);
  and and_2 (and_2_out, and_3_out, not_3_out);
  xor xor_3 (s3, not_3_out, and_3_out);
  not not_3 (not_3_out, a3);
  and and_3 (and_3_out, and_4_out, not_4_out);
  xor xor_4 (s2, not_4_out, and_4_out);
  not not_4 (not_4_out, a2);
  and and_4 (and_4_out, and_5_out, not_5_out);
  xor xor_5 (s1, not_5_out, and_5_out);
  not not_5 (not_5_out, a1);
  and and_5 (and_5_out, not_6_out, 1'b1);
  xor xor_6 (s0, not_6_out, 1'b1);
  not not_6 (not_6_out, a0);

  assign s6 = 1'b1;
endmodule

module _02 (
  input  a3,
  input  a2,
  input  a1,
  input  a0,
  input  b3,
  input  b2,
  input  b1,
  input  b0,
  output s4,
  output s2,
  output s1,
  output s0
);

  wire and_1_out, and_2_out, and_3_out, and_4_out, and_5_out, and_6_out, not_1_out, not_2_out, not_3_out,
       not_4_out, not_5_out, not_6_out, or_1_out, or_2_out, or_3_out, xor_2_out, xor_4_out, xor_6_out,
       xor_8_out;

  xor xor_1 (s4, xor_2_out, or_1_out);
  xor xor_2 (xor_2_out, b3, a3);
  or or_1 (or_1_out, and_2_out, and_1_out);
  and and_1 (and_1_out, or_2_out, not_1_out);
  xor xor_3 (s2, xor_4_out, or_2_out);
  and and_2 (and_2_out, b2, not_2_out);
  not not_1 (not_1_out, xor_4_out);
  xor xor_4 (xor_4_out, b2, a2);
  not not_2 (not_2_out, a2);
  or or_2 (or_2_out, and_4_out, and_3_out);
  and and_3 (and_3_out, or_3_out, not_3_out);
  xor xor_5 (s1, xor_6_out, or_3_out);
  and and_4 (and_4_out, b1, not_4_out);
  not not_3 (not_3_out, xor_6_out);
  xor xor_6 (xor_6_out, b1, a1);
  or or_3 (or_3_out, and_6_out, and_5_out);
  not not_4 (not_4_out, a1);
  and and_5 (and_5_out, 1'b0, not_5_out);
  not not_5 (not_5_out, xor_8_out);
  xor xor_7 (s0, xor_8_out, 1'b0);
  and and_6 (and_6_out, b0, not_6_out);
  xor xor_8 (xor_8_out, b0, a0);
  not not_6 (not_6_out, a0);
endmodule
