// Logisim project Guia_12.circ as structural Verilog: 4 circuits, main circuit Guia_1201
// 1x4
module Guia_1201 (
  input  [3:0] in_1,
  input  CLK,
  input  R_W,
  input  Addr,
  input  CLR,
  output [3:0] out_6
);

  wire and_1_out, and_2_out, j_k_ff_1_q, j_k_ff_2_q, j_k_ff_3_q, j_k_ff_4_q, not_1_out, not_2_out, not_3_out,
       not_4_out, not_5_out, not_6_out;

  and and_1 (and_1_out, CLK, R_W, Addr);
  not not_1 (not_1_out, in_1[3]);
  not not_2 (not_2_out, CLK);
  and and_2 (and_2_out, not_2_out, Addr, not_3_out);
  not not_3 (not_3_out, R_W);
  J_K_Flip_Flop #(.Pre_Clr_Positions("LEGACY"), .NewFFLayout("false")) j_k_ff_1 (
    .J(in_1[3]), .clk(and_1_out), .K(not_1_out), .Q(j_k_ff_1_q), .reset(CLR));  // open: Qn, preset
  not not_4 (not_4_out, in_1[2]);
  J_K_Flip_Flop #(.Pre_Clr_Positions("LEGACY"), .NewFFLayout("false")) j_k_ff_2 (
    .J(in_1[2]), .clk(and_1_out), .K(not_4_out), .Q(j_k_ff_2_q), .reset(CLR));  // open: Qn, preset
  not not_5 (not_5_out, in_1[1]);
  and and_3 (out_6[3], j_k_ff_1_q, and_2_out);
  J_K_Flip_Flop #(.Pre_Clr_Positions("LEGACY"), .NewFFLayout("false")) j_k_ff_3 (
    .J(in_1[1]), .clk(and_1_out), .K(not_5_out), .Q(j_k_ff_3_q), .reset(CLR));  // open: Qn, preset
  not not_6 (not_6_out, in_1[0]);
  and and_4 (out_6[2], j_k_ff_2_q, and_2_out);
  J_K_Flip_Flop #(.Pre_Clr_Positions("LEGACY"), .NewFFLayout("false")) j_k_ff_4 (
    .J(in_1[0]), .clk(and_1_out), .K(not_6_out), .Q(j_k_ff_4_q), .reset(CLR));  // open: Qn, preset
  and and_5 (out_6[1], j_k_ff_3_q, and_2_out);
  and and_6 (out_6[0], j_k_ff_4_q, and_2_out);
endmodule

// 2(1x4)
module Guia_1202 (
  input  [7:0] in_1,
  input  CLK,
  input  R_W,
  input  Addr,
  input  CLR,
  output [7:0] out_6
);

  wire and_1_out, and_2_out, and_3_out, and_4_out, j_k_ff_1_q, j_k_ff_2_q, j_k_ff_3_q, j_k_ff_4_q,
       j_k_ff_5_q, j_k_ff_6_q, j_k_ff_7_q, j_k_ff_8_q, not_1_out, not_2_out, not_3_out, not_4_out, not_5_out,
       not_6_out, not_7_out, not_8_out, not_9_out, not_10_out, not_11_out, not_12_out;

  and and_1 (and_1_out, CLK, R_W, Addr);
  not not_1 (not_1_out, in_1[3]);
  not not_2 (not_2_out, CLK);
  and and_2 (and_2_out, not_2_out, Addr, not_3_out);
  not not_3 (not_3_out, R_W);
  and and_3 (and_3_out, CLK, R_W, Addr);
  not not_4 (not_4_out, in_1[7]);
  not not_5 (not_5_out, CLK);
  and and_4 (and_4_out, not_5_out, Addr, not_6_out);
  not not_6 (not_6_out, R_W);
  J_K_Flip_Flop #(.Pre_Clr_Positions("LEGACY"), .NewFFLayout("false")) j_k_ff_1 (
    .J(in_1[3]), .clk(and_1_out), .K(not_1_out), .Q(j_k_ff_1_q), .reset(CLR));  // open: Qn, preset
  not not_7 (not_7_out, in_1[2]);
  and and_5 (out_6[3], j_k_ff_1_q, and_2_out);
  J_K_Flip_Flop #(.Pre_Clr_Positions("LEGACY"), .NewFFLayout("false")) j_k_ff_2 (
    .J(in_1[7]), .clk(and_3_out), .K(not_4_out), .Q(j_k_ff_2_q), .reset(CLR));  // open: Qn, preset
  not not_8 (not_8_out, in_1[6]);
  and and_6 (out_6[7], j_k_ff_2_q, and_4_out);
  J_K_Flip_Flop #(.Pre_Clr_Positions("LEGACY"), .NewFFLayout("false")) j_k_ff_3 (
    .J(in_1[2]), .clk(and_1_out), .K(not_7_out), .Q(j_k_ff_3_q), .reset(CLR));  // open: Qn, preset
  not not_9 (not_9_out, in_1[1]);
  and and_7 (out_6[2], j_k_ff_3_q, and_2_out);
  J_K_Flip_Flop #(.Pre_Clr_Positions("LEGACY"), .NewFFLayout("false")) j_k_ff_4 (
    .J(in_1[6]), .clk(and_3_out), .K(not_8_out), .Q(j_k_ff_4_q), .reset(CLR));  // open: Qn, preset
  not not_10 (not_10_out, in_1[5]);
  and and_8 (out_6[6], j_k_ff_4_q, and_4_out);
  J_K_Flip_Flop #(.Pre_Clr_Positions("LEGACY"), .NewFFLayout("false")) j_k_ff_5 (
    .J(in_1[1]), .clk(and_1_out), .K(not_9_out), .Q(j_k_ff_5_q), .reset(CLR));  // open: Qn, preset
  not not_11 (not_11_out, in_1[0]);
  and and_9 (out_6[1], j_k_ff_5_q, and_2_out);
  J_K_Flip_Flop #(.Pre_Clr_Positions("LEGACY"), .NewFFLayout("false")) j_k_ff_6 (
    .J(in_1[5]), .clk(and_3_out), .K(not_10_out), .Q(j_k_ff_6_q), .reset(CLR));  // open: Qn, preset
  not not_12 (not_12_out, in_1[4]);
  and and_10 (out_6[5], j_k_ff_6_q, and_4_out);
  J_K_Flip_Flop #(.Pre_Clr_Positions("LEGACY"), .NewFFLayout("false")) j_k_ff_7 (
    .J(in_1[0]), .clk(and_1_out), .K(not_11_out), .Q(j_k_ff_7_q), .reset(CLR));  // open: Qn, preset
  and and_11 (out_6[0], j_k_ff_7_q, and_2_out);
  J_K_Flip_Flop #(.Pre_Clr_Positions("LEGACY"), .NewFFLayout("false")) j_k_ff_8 (
    .J(in_1[4]), .clk(and_3_out), .K(not_12_out), .Q(j_k_ff_8_q), .reset(CLR));  // open: Qn, preset
  and and_12 (out_6[4], j_k_ff_8_q, and_4_out);
endmodule

// 2x8
module Guia_1203 (
  input  CLK,
  input  [7:0] in_2,
  input  R_W,
  input  Addr,
  input  CLR,
  output [7:0] out_6
);

  wire and_1_out, and_2_out, and_3_out, and_4_out, j_k_ff_1_q, j_k_ff_2_q, j_k_ff_3_q, j_k_ff_4_q,
       j_k_ff_5_q, j_k_ff_6_q, j_k_ff_7_q, j_k_ff_8_q, j_k_ff_9_q, j_k_ff_10_q, j_k_ff_11_q, j_k_ff_12_q,
       j_k_ff_13_q, j_k_ff_14_q, j_k_ff_15_q, j_k_ff_16_q, not_1_out, not_2_out, not_3_out, not_4_out,
       not_5_out, not_6_out, not_7_out, not_8_out, not_9_out, not_10_out, not_11_out, not_12_out, not_13_out,
       not_14_out, not_15_out, not_16_out, not_17_out, not_18_out, not_19_out, not_20_out, not_21_out;
  wire [7:0] and_19_out, and_20_out;

  not not_1 (not_1_out, Addr);
  and and_1 (and_1_out, CLK, R_W, not_1_out);
  not not_2 (not_2_out, in_2[7]);
  not not_3 (not_3_out, CLK);
  and and_2 (and_2_out, not_3_out, not_1_out, not_4_out);
  not not_4 (not_4_out, R_W);
  and and_3 (and_3_out, CLK, R_W, Addr);
  not not_5 (not_5_out, in_2[7]);
  not not_6 (not_6_out, CLK);
  and and_4 (and_4_out, not_6_out, Addr, not_7_out);
  not not_7 (not_7_out, R_W);
  J_K_Flip_Flop #(.Pre_Clr_Positions("LEGACY"), .NewFFLayout("false")) j_k_ff_1 (
    .J(in_2[7]), .clk(and_1_out), .K(not_2_out), .Q(j_k_ff_1_q), .reset(CLR));  // open: Qn, preset
  not not_8 (not_8_out, in_2[6]);
  J_K_Flip_Flop #(.Pre_Clr_Positions("LEGACY"), .NewFFLayout("false")) j_k_ff_2 (
    .J(in_2[7]), .clk(and_3_out), .K(not_5_out), .Q(j_k_ff_2_q), .reset(CLR));  // open: Qn, preset
  not not_9 (not_9_out, in_2[6]);
  J_K_Flip_Flop #(.Pre_Clr_Positions("LEGACY"), .NewFFLayout("false")) j_k_ff_3 (
    .J(in_2[6]), .clk(and_1_out), .K(not_8_out), .Q(j_k_ff_3_q), .reset(CLR));  // open: Qn, preset
  not not_10 (not_10_out, in_2[5]);
  and and_5 (and_19_out[7], j_k_ff_1_q, and_2_out);
  J_K_Flip_Flop #(.Pre_Clr_Positions("LEGACY"), .NewFFLayout("false")) j_k_ff_4 (
    .J(in_2[6]), .clk(and_3_out), .K(not_9_out), .Q(j_k_ff_4_q), .reset(CLR));  // open: Qn, preset
  not not_11 (not_11_out, in_2[5]);
  and and_6 (and_20_out[7], j_k_ff_2_q, and_4_out);
  J_K_Flip_Flop #(.Pre_Clr_Positions("LEGACY"), .NewFFLayout("false")) j_k_ff_5 (
    .J(in_2[5]), .clk(and_1_out), .K(not_10_out), .Q(j_k_ff_5_q), .reset(CLR));  // open: Qn, preset
  not not_12 (not_12_out, in_2[4]);
  and and_7 (and_19_out[6], j_k_ff_3_q, and_2_out);
  J_K_Flip_Flop #(.Pre_Clr_Positions("LEGACY"), .NewFFLayout("false")) j_k_ff_6 (
    .J(in_2[5]), .clk(and_3_out), .K(not_11_out), .Q(j_k_ff_6_q), .reset(CLR));  // open: Qn, preset
  not not_13 (not_13_out, in_2[4]);
  and and_8 (and_20_out[6], j_k_ff_4_q, and_4_out);
  J_K_Flip_Flop #(.Pre_Clr_Positions("LEGACY"), .NewFFLayout("false")) j_k_ff_7 (
    .J(in_2[4]), .clk(and_1_out), .K(not_12_out), .Q(j_k_ff_7_q), .reset(CLR));  // open: Qn, preset
  not not_14 (not_14_out, in_2[3]);
  and and_9 (and_19_out[5], j_k_ff_5_q, and_2_out);
  J_K_Flip_Flop #(.Pre_Clr_Positions("LEGACY"), .NewFFLayout("false")) j_k_ff_8 (
    .J(in_2[4]), .clk(and_3_out), .K(not_13_out), .Q(j_k_ff_8_q), .reset(CLR));  // open: Qn, preset
  not not_15 (not_15_out, in_2[3]);
  and and_10 (and_20_out[5], j_k_ff_6_q, and_4_out);
  J_K_Flip_Flop #(.Pre_Clr_Positions("LEGACY"), .NewFFLayout("false")) j_k_ff_9 (
    .J(in_2[3]), .clk(and_1_out), .K(not_14_out), .Q(j_k_ff_9_q), .reset(CLR));  // open: Qn, preset
  not not_16 (not_16_out, in_2[2]);
  and and_11 (and_19_out[4], j_k_ff_7_q, and_2_out);
  J_K_Flip_Flop #(.Pre_Clr_Positions("LEGACY"), .NewFFLayout("false")) j_k_ff_10 (
    .J(in_2[3]), .clk(and_3_out), .K(not_15_out), .Q(j_k_ff_10_q), .reset(CLR));  // open: Qn, preset
  not not_17 (not_17_out, in_2[2]);
  and and_12 (and_20_out[4], j_k_ff_8_q, and_4_out);
  J_K_Flip_Flop #(.Pre_Clr_Positions("LEGACY"), .NewFFLayout("false")) j_k_ff_11 (
    .J(in_2[2]), .clk(and_1_out), .K(not_16_out), .Q(j_k_ff_11_q), .reset(CLR));  // open: Qn, preset
  not not_18 (not_18_out, in_2[1]);
  and and_13 (and_19_out[3], j_k_ff_9_q, and_2_out);
  J_K_Flip_Flop #(.Pre_Clr_Positions("LEGACY"), .NewFFLayout("false")) j_k_ff_12 (
    .J(in_2[2]), .clk(and_3_out), .K(not_17_out), .Q(j_k_ff_12_q), .reset(CLR));  // open: Qn, preset
  not not_19 (not_19_out, in_2[1]);
  and and_14 (and_20_out[3], j_k_ff_10_q, and_4_out);
  J_K_Flip_Flop #(.Pre_Clr_Positions("LEGACY"), .NewFFLayout("false")) j_k_ff_13 (
    .J(in_2[1]), .clk(and_1_out), .K(not_18_out), .Q(j_k_ff_13_q), .reset(CLR));  // open: Qn, preset
  not not_20 (not_20_out, in_2[0]);
  and and_15 (and_19_out[2], j_k_ff_11_q, and_2_out);
  J_K_Flip_Flop #(.Pre_Clr_Positions("LEGACY"), .NewFFLayout("false")) j_k_ff_14 (
    .J(in_2[1]), .clk(and_3_out), .K(not_19_out), .Q(j_k_ff_14_q), .reset(CLR));  // open: Qn, preset
  not not_21 (not_21_out, in_2[0]);
  and and_16 (and_20_out[2], j_k_ff_12_q, and_4_out);
  J_K_Flip_Flop #(.Pre_Clr_Positions("LEGACY"), .NewFFLayout("false")) j_k_ff_15 (
    .J(in_2[0]), .clk(and_1_out), .K(not_20_out), .Q(j_k_ff_15_q), .reset(CLR));  // open: Qn, preset
  and and_17 (and_19_out[1], j_k_ff_13_q, and_2_out);
  J_K_Flip_Flop #(.Pre_Clr_Positions("LEGACY"), .NewFFLayout("false")) j_k_ff_16 (
    .J(in_2[0]), .clk(and_3_out), .K(not_21_out), .Q(j_k_ff_16_q), .reset(CLR));  // open: Qn, preset
  and and_18 (and_20_out[1], j_k_ff_14_q, and_4_out);
  and and_19 (and_19_out[0], j_k_ff_15_q, and_2_out);
  and and_20 (and_20_out[0], j_k_ff_16_q, and_4_out);
  Multiplexer #(.width(8), .enable("false")) multiplexer_1 (
    .in0(and_19_out), .in1(and_20_out), .out(out_6), .sel(Addr));
endmodule

module Guia_1204 (
  input  CLK,
  input  R_W,
  input  [1:0] Addr,
  input  [7:0] in_4,
  input  CLR,
  output [7:0] out_6
);

  wire and_1_out, and_2_out, and_3_out, and_4_out, and_5_out, and_6_out, and_7_out, and_8_out, and_9_out,
       and_10_out, and_11_out, j_k_ff_1_q, j_k_ff_2_q, j_k_ff_3_q, j_k_ff_4_q, j_k_ff_5_q, j_k_ff_6_q,
       j_k_ff_7_q, j_k_ff_8_q, j_k_ff_9_q, j_k_ff_10_q, j_k_ff_11_q, j_k_ff_12_q, j_k_ff_13_q, j_k_ff_14_q,
       j_k_ff_15_q, j_k_ff_16_q, j_k_ff_17_q, j_k_ff_18_q, j_k_ff_19_q, j_k_ff_20_q, j_k_ff_21_q,
       j_k_ff_22_q, j_k_ff_23_q, j_k_ff_24_q, j_k_ff_25_q, j_k_ff_26_q, j_k_ff_27_q, j_k_ff_28_q,
       j_k_ff_29_q, j_k_ff_30_q, j_k_ff_31_q, j_k_ff_32_q, not_1_out, not_2_out, not_3_out, not_4_out,
       not_5_out, not_6_out, not_7_out, not_8_out, not_9_out, not_10_out, not_11_out, not_12_out, not_13_out,
       not_14_out, not_15_out, not_16_out, not_17_out, not_18_out, not_19_out, not_20_out, not_21_out,
       not_22_out, not_23_out, not_24_out, not_25_out, not_26_out, not_27_out, not_28_out, not_29_out,
       not_30_out, not_31_out, not_32_out, not_33_out, not_34_out, not_35_out, not_36_out, not_37_out,
       not_38_out, not_39_out, not_40_out, not_41_out, not_42_out, not_43_out, not_44_out, not_45_out,
       or_1_out;
  wire [7:0] and_40_out, and_41_out, and_42_out, and_43_out, demultiplexer_1_out0, demultiplexer_1_out1,
       multiplexer_2_out, multiplexer_3_out;

  not not_1 (not_1_out, Addr[0]);
  and and_1 (and_1_out, not_1_out, not_2_out);
  not not_2 (not_2_out, Addr[1]);
  and and_2 (and_2_out, Addr[0], not_3_out);
  not not_3 (not_3_out, Addr[1]);
  and and_3 (and_3_out, Addr[0], Addr[1]);
  or or_1 (or_1_out, and_1_out, and_2_out);
  Demultiplexer #(.width(8), .enable("false")) demultiplexer_1 (
    .out0(demultiplexer_1_out0), .out1(demultiplexer_1_out1), .in(in_4), .sel(or_1_out));
  Multiplexer #(.width(8), .enable("false")) multiplexer_1 (
    .in0(multiplexer_3_out), .in1(multiplexer_2_out), .out(out_6), .sel(or_1_out));
  not not_4 (not_4_out, and_2_out);
  not not_5 (not_5_out, and_3_out);
  and and_4 (and_4_out, CLK, R_W, not_4_out);
  not not_6 (not_6_out, demultiplexer_1_out1[7]);
  not not_7 (not_7_out, CLK);
  and and_5 (and_5_out, not_7_out, not_4_out, not_8_out);
  not not_8 (not_8_out, R_W);
  and and_6 (and_6_out, CLK, R_W, and_2_out);
  not not_9 (not_9_out, demultiplexer_1_out1[7]);
  not not_10 (not_10_out, CLK);
  and and_7 (and_7_out, not_10_out, and_2_out, not_11_out);
  not not_11 (not_11_out, R_W);
  and and_8 (and_8_out, CLK, R_W, not_5_out);
  not not_12 (not_12_out, demultiplexer_1_out0[7]);
  not not_13 (not_13_out, CLK);
  and and_9 (and_9_out, not_13_out, not_5_out, not_14_out);
  not not_14 (not_14_out, R_W);
  and and_10 (and_10_out, CLK, R_W, and_3_out);
  not not_15 (not_15_out, demultiplexer_1_out0[7]);
  not not_16 (not_16_out, CLK);
  and and_11 (and_11_out, not_16_out, and_3_out, not_17_out);
  not not_17 (not_17_out, R_W);
  J_K_Flip_Flop #(.Pre_Clr_Positions("LEGACY"), .NewFFLayout("false")) j_k_ff_1 (
    .J(demultiplexer_1_out1[7]), .clk(and_4_out), .K(not_6_out), .Q(j_k_ff_1_q), .reset(CLR));  // open: Qn, preset
  not not_18 (not_18_out, demultiplexer_1_out1[6]);
  and and_12 (and_40_out[7], j_k_ff_1_q, and_5_out);
  J_K_Flip_Flop #(.Pre_Clr_Positions("LEGACY"), .NewFFLayout("false")) j_k_ff_2 (
    .J(demultiplexer_1_out1[7]), .clk(and_6_out), .K(not_9_out), .Q(j_k_ff_2_q), .reset(CLR));  // open: Qn, preset
  not not_19 (not_19_out, demultiplexer_1_out1[6]);
  and and_13 (and_41_out[7], j_k_ff_2_q, and_7_out);
  J_K_Flip_Flop #(.Pre_Clr_Positions("LEGACY"), .NewFFLayout("false")) j_k_ff_3 (
    .J(demultiplexer_1_out0[7]), .clk(and_8_out), .K(not_12_out), .Q(j_k_ff_3_q), .reset(CLR));  // open: Qn, preset
  not not_20 (not_20_out, demultiplexer_1_out0[6]);
  and and_14 (and_42_out[7], j_k_ff_3_q, and_9_out);
  J_K_Flip_Flop #(.Pre_Clr_Positions("LEGACY"), .NewFFLayout("false")) j_k_ff_4 (
    .J(demultiplexer_1_out0[7]), .clk(and_10_out), .K(not_15_out), .Q(j_k_ff_4_q), .reset(CLR));  // open: Qn, preset
  not not_21 (not_21_out, demultiplexer_1_out0[6]);
  and and_15 (and_43_out[7], j_k_ff_4_q, and_11_out);
  J_K_Flip_Flop #(.Pre_Clr_Positions("LEGACY"), .NewFFLayout("false")) j_k_ff_5 (
    .J(demultiplexer_1_out1[6]), .clk(and_4_out), .K(not_18_out), .Q(j_k_ff_5_q), .reset(CLR));  // open: Qn, preset
  not not_22 (not_22_out, demultiplexer_1_out1[5]);
  and and_16 (and_40_out[6], j_k_ff_5_q, and_5_out);
  J_K_Flip_Flop #(.Pre_Clr_Positions("LEGACY"), .NewFFLayout("false")) j_k_ff_6 (
    .J(demultiplexer_1_out1[6]), .clk(and_6_out), .K(not_19_out), .Q(j_k_ff_6_q), .reset(CLR));  // open: Qn, preset
  not not_23 (not_23_out, demultiplexer_1_out1[5]);
  and and_17 (and_41_out[6], j_k_ff_6_q, and_7_out);
  J_K_Flip_Flop #(.Pre_Clr_Positions("LEGACY"), .NewFFLayout("false")) j_k_ff_7 (
    .J(demultiplexer_1_out0[6]), .clk(and_8_out), .K(not_20_out), .Q(j_k_ff_7_q), .reset(CLR));  // open: Qn, preset
  not not_24 (not_24_out, demultiplexer_1_out0[5]);
  and and_18 (and_42_out[6], j_k_ff_7_q, and_9_out);
  J_K_Flip_Flop #(.Pre_Clr_Positions("LEGACY"), .NewFFLayout("false")) j_k_ff_8 (
    .J(demultiplexer_1_out0[6]), .clk(and_10_out), .K(not_21_out), .Q(j_k_ff_8_q), .reset(CLR));  // open: Qn, preset
  not not_25 (not_25_out, demultiplexer_1_out0[5]);
  and and_19 (and_43_out[6], j_k_ff_8_q, and_11_out);
  J_K_Flip_Flop #(.Pre_Clr_Positions("LEGACY"), .NewFFLayout("false")) j_k_ff_9 (
    .J(demultiplexer_1_out1[5]), .clk(and_4_out), .K(not_22_out), .Q(j_k_ff_9_q), .reset(CLR));  // open: Qn, preset
  not not_26 (not_26_out, demultiplexer_1_out1[4]);
  and and_20 (and_40_out[5], j_k_ff_9_q, and_5_out);
  J_K_Flip_Flop #(.Pre_Clr_Positions("LEGACY"), .NewFFLayout("false")) j_k_ff_10 (
    .J(demultiplexer_1_out1[5]), .clk(and_6_out), .K(not_23_out), .Q(j_k_ff_10_q), .reset(CLR));  // open: Qn, preset
  not not_27 (not_27_out, demultiplexer_1_out1[4]);
  and and_21 (and_41_out[5], j_k_ff_10_q, and_7_out);
  J_K_Flip_Flop #(.Pre_Clr_Positions("LEGACY"), .NewFFLayout("false")) j_k_ff_11 (
    .J(demultiplexer_1_out0[5]), .clk(and_8_out), .K(not_24_out), .Q(j_k_ff_11_q), .reset(CLR));  // open: Qn, preset
  not not_28 (not_28_out, demultiplexer_1_out0[4]);
  and and_22 (and_42_out[5], j_k_ff_11_q, and_9_out);
  J_K_Flip_Flop #(.Pre_Clr_Positions("LEGACY"), .NewFFLayout("false")) j_k_ff_12 (
    .J(demultiplexer_1_out0[5]), .clk(and_10_out), .K(not_25_out), .Q(j_k_ff_12_q), .reset(CLR));  // open: Qn, preset
  not not_29 (not_29_out, demultiplexer_1_out0[4]);
  and and_23 (and_43_out[5], j_k_ff_12_q, and_11_out);
  J_K_Flip_Flop #(.Pre_Clr_Positions("LEGACY"), .NewFFLayout("false")) j_k_ff_13 (
    .J(demultiplexer_1_out1[4]), .clk(and_4_out), .K(not_26_out), .Q(j_k_ff_13_q), .reset(CLR));  // open: Qn, preset
  not not_30 (not_30_out, demultiplexer_1_out1[3]);
  and and_24 (and_40_out[4], j_k_ff_13_q, and_5_out);
  J_K_Flip_Flop #(.Pre_Clr_Positions("LEGACY"), .NewFFLayout("false")) j_k_ff_14 (
    .J(demultiplexer_1_out1[4]), .clk(and_6_out), .K(not_27_out), .Q(j_k_ff_14_q), .reset(CLR));  // open: Qn, preset
  not not_31 (not_31_out, demultiplexer_1_out1[3]);
  and and_25 (and_41_out[4], j_k_ff_14_q, and_7_out);
  J_K_Flip_Flop #(.Pre_Clr_Positions("LEGACY"), .NewFFLayout("false")) j_k_ff_15 (
    .J(demultiplexer_1_out0[4]), .clk(and_8_out), .K(not_28_out), .Q(j_k_ff_15_q), .reset(CLR));  // open: Qn, preset
  not not_32 (not_32_out, demultiplexer_1_out0[3]);
  and and_26 (and_42_out[4], j_k_ff_15_q, and_9_out);
  J_K_Flip_Flop #(.Pre_Clr_Positions("LEGACY"), .NewFFLayout("false")) j_k_ff_16 (
    .J(demultiplexer_1_out0[4]), .clk(and_10_out), .K(not_29_out), .Q(j_k_ff_16_q), .reset(CLR));  // open: Qn, preset
  not not_33 (not_33_out, demultiplexer_1_out0[3]);
  and and_27 (and_43_out[4], j_k_ff_16_q, and_11_out);
  J_K_Flip_Flop #(.Pre_Clr_Positions("LEGACY"), .NewFFLayout("false")) j_k_ff_17 (
    .J(demultiplexer_1_out1[3]), .clk(and_4_out), .K(not_30_out), .Q(j_k_ff_17_q), .reset(CLR));  // open: Qn, preset
  not not_34 (not_34_out, demultiplexer_1_out1[2]);
  and and_28 (and_40_out[3], j_k_ff_17_q, and_5_out);
  J_K_Flip_Flop #(.Pre_Clr_Positions("LEGACY"), .NewFFLayout("false")) j_k_ff_18 (
    .J(demultiplexer_1_out1[3]), .clk(and_6_out), .K(not_31_out), .Q(j_k_ff_18_q), .reset(CLR));  // open: Qn, preset
  not not_35 (not_35_out, demultiplexer_1_out1[2]);
  and and_29 (and_41_out[3], j_k_ff_18_q, and_7_out);
  J_K_Flip_Flop #(.Pre_Clr_Positions("LEGACY"), .NewFFLayout("false")) j_k_ff_19 (
    .J(demultiplexer_1_out0[3]), .clk(and_8_out), .K(not_32_out), .Q(j_k_ff_19_q), .reset(CLR));  // open: Qn, preset
  not not_36 (not_36_out, demultiplexer_1_out0[2]);
  and and_30 (and_42_out[3], j_k_ff_19_q, and_9_out);
  J_K_Flip_Flop #(.Pre_Clr_Positions("LEGACY"), .NewFFLayout("false")) j_k_ff_20 (
    .J(demultiplexer_1_out0[3]), .clk(and_10_out), .K(not_33_out), .Q(j_k_ff_20_q), .reset(CLR));  // open: Qn, preset
  not not_37 (not_37_out, demultiplexer_1_out0[2]);
  and and_31 (and_43_out[3], j_k_ff_20_q, and_11_out);
  J_K_Flip_Flop #(.Pre_Clr_Positions("LEGACY"), .NewFFLayout("false")) j_k_ff_21 (
    .J(demultiplexer_1_out1[2]), .clk(and_4_out), .K(not_34_out), .Q(j_k_ff_21_q), .reset(CLR));  // open: Qn, preset
  not not_38 (not_38_out, demultiplexer_1_out1[1]);
  and and_32 (and_40_out[2], j_k_ff_21_q, and_5_out);
  J_K_Flip_Flop #(.Pre_Clr_Positions("LEGACY"), .NewFFLayout("false")) j_k_ff_22 (
    .J(demultiplexer_1_out1[2]), .clk(and_6_out), .K(not_35_out), .Q(j_k_ff_22_q), .reset(CLR));  // open: Qn, preset
  not not_39 (not_39_out, demultiplexer_1_out1[1]);
  and and_33 (and_41_out[2], j_k_ff_22_q, and_7_out);
  J_K_Flip_Flop #(.Pre_Clr_Positions("LEGACY"), .NewFFLayout("false")) j_k_ff_23 (
    .J(demultiplexer_1_out0[2]), .clk(and_8_out), .K(not_36_out), .Q(j_k_ff_23_q), .reset(CLR));  // open: Qn, preset
  not not_40 (not_40_out, demultiplexer_1_out0[1]);
  and and_34 (and_42_out[2], j_k_ff_23_q, and_9_out);
  J_K_Flip_Flop #(.Pre_Clr_Positions("LEGACY"), .NewFFLayout("false")) j_k_ff_24 (
    .J(demultiplexer_1_out0[2]), .clk(and_10_out), .K(not_37_out), .Q(j_k_ff_24_q), .reset(CLR));  // open: Qn, preset
  not not_41 (not_41_out, demultiplexer_1_out0[1]);
  and and_35 (and_43_out[2], j_k_ff_24_q, and_11_out);
  J_K_Flip_Flop #(.Pre_Clr_Positions("LEGACY"), .NewFFLayout("false")) j_k_ff_25 (
    .J(demultiplexer_1_out1[1]), .clk(and_4_out), .K(not_38_out), .Q(j_k_ff_25_q), .reset(CLR));  // open: Qn, preset
  not not_42 (not_42_out, demultiplexer_1_out1[0]);
  and and_36 (and_40_out[1], j_k_ff_25_q, and_5_out);
  J_K_Flip_Flop #(.Pre_Clr_Positions("LEGACY"), .NewFFLayout("false")) j_k_ff_26 (
    .J(demultiplexer_1_out1[1]), .clk(and_6_out), .K(not_39_out), .Q(j_k_ff_26_q), .reset(CLR));  // open: Qn, preset
  not not_43 (not_43_out, demultiplexer_1_out1[0]);
  and and_37 (and_41_out[1], j_k_ff_26_q, and_7_out);
  J_K_Flip_Flop #(.Pre_Clr_Positions("LEGACY"), .NewFFLayout("false")) j_k_ff_27 (
    .J(demultiplexer_1_out0[1]), .clk(and_8_out), .K(not_40_out), .Q(j_k_ff_27_q), .reset(CLR));  // open: Qn, preset
  not not_44 (not_44_out, demultiplexer_1_out0[0]);
  and and_38 (and_42_out[1], j_k_ff_27_q, and_9_out);
  J_K_Flip_Flop #(.Pre_Clr_Positions("LEGACY"), .NewFFLayout("false")) j_k_ff_28 (
    .J(demultiplexer_1_out0[1]), .clk(and_10_out), .K(not_41_out), .Q(j_k_ff_28_q), .reset(CLR));  // open: Qn, preset
  not not_45 (not_45_out, demultiplexer_1_out0[0]);
  and and_39 (and_43_out[1], j_k_ff_28_q, and_11_out);
  J_K_Flip_Flop #(.Pre_Clr_Positions("LEGACY"), .NewFFLayout("false")) j_k_ff_29 (
    .J(demultiplexer_1_out1[0]), .clk(and_4_out), .K(not_42_out), .Q(j_k_ff_29_q), .reset(CLR));  // open: Qn, preset
  and and_40 (and_40_out[0], j_k_ff_29_q, and_5_out);
  J_K_Flip_Flop #(.Pre_Clr_Positions("LEGACY"), .NewFFLayout("false")) j_k_ff_30 (
    .J(demultiplexer_1_out1[0]), .clk(and_6_out), .K(not_43_out), .Q(j_k_ff_30_q), .reset(CLR));  // open: Qn, preset
  and and_41 (and_41_out[0], j_k_ff_30_q, and_7_out);
  J_K_Flip_Flop #(.Pre_Clr_Positions("LEGACY"), .NewFFLayout("false")) j_k_ff_31 (
    .J(demultiplexer_1_out0[0]), .clk(and_8_out), .K(not_44_out), .Q(j_k_ff_31_q), .reset(CLR));  // open: Qn, preset
  and and_42 (and_42_out[0], j_k_ff_31_q, and_9_out);
  J_K_Flip_Flop #(.Pre_Clr_Positions("LEGACY"), .NewFFLayout("false")) j_k_ff_32 (
    .J(demultiplexer_1_out0[0]), .clk(and_10_out), .K(not_45_out), .Q(j_k_ff_32_q), .reset(CLR));  // open: Qn, preset
  and and_43 (and_43_out[0], j_k_ff_32_q, and_11_out);
  Multiplexer #(.width(8), .enable("false")) multiplexer_2 (
    .in0(and_40_out), .in1(and_41_out), .out(multiplexer_2_out), .sel(and_2_out));
  Multiplexer #(.width(8), .enable("false")) multiplexer_3 (
    .in0(and_42_out), .in1(and_43_out), .out(multiplexer_3_out), .sel(and_3_out));
endmodule
