// Logisim project Guia_13.circ as structural Verilog: 5 circuits, main circuit Guia_1301
module Guia_1301 (
  input  in_1,
  input  in_2,
  input  in_3
);

  wire j_k_ff_1_qn, j_k_ff_2_qn, j_k_ff_3_qn, j_k_ff_4_qn, j_k_ff_5_qn;

  // Probe on j_k_ff_1_qn
  J_K_Flip_Flop #(.Pre_Clr_Positions("LEGACY"), .NewFFLayout("false")) j_k_ff_1 (
    .J(in_2), .clk(j_k_ff_2_qn), .K(in_2), .Qn(j_k_ff_1_qn), .reset(in_3));  // open: Q, preset
  // Probe on j_k_ff_2_qn
  J_K_Flip_Flop #(.Pre_Clr_Positions("LEGACY"), .NewFFLayout("false")) j_k_ff_2 (
    .J(in_2), .clk(j_k_ff_3_qn), .K(in_2), .Qn(j_k_ff_2_qn), .reset(in_3));  // open: Q, preset
  // Probe on j_k_ff_3_qn
  J_K_Flip_Flop #(.Pre_Clr_Positions("LEGACY"), .NewFFLayout("false")) j_k_ff_3 (
    .J(in_2), .clk(j_k_ff_4_qn), .K(in_2), .Qn(j_k_ff_3_qn), .reset(in_3));  // open: Q, preset
  J_K_Flip_Flop #(.Pre_Clr_Positions("LEGACY"), .NewFFLayout("false")) j_k_ff_4 (
    .J(in_2), .clk(j_k_ff_5_qn), .K(in_2), .Qn(j_k_ff_4_qn), .reset(in_3));  // open: Q, preset
  // Probe on j_k_ff_4_qn
  // Probe on j_k_ff_5_qn
  J_K_Flip_Flop #(.Pre_Clr_Positions("LEGACY"), .NewFFLayout("false")) j_k_ff_5 (
    .J(in_2), .clk(in_1), .K(in_2), .Qn(j_k_ff_5_qn), .reset(in_3));  // open: Q, preset
endmodule

module Guia_1302 (
  input  in_1,
  input  in_2,
  input  in_3
);

  wire j_k_ff_1_qn, j_k_ff_2_q, j_k_ff_2_qn, j_k_ff_3_q, j_k_ff_3_qn, j_k_ff_4_q, j_k_ff_4_qn, j_k_ff_5_q,
       j_k_ff_5_qn;

  // Probe on j_k_ff_1_qn
  J_K_Flip_Flop #(.Pre_Clr_Positions("LEGACY"), .NewFFLayout("false")) j_k_ff_1 (
    .J(in_2), .clk(j_k_ff_2_q), .K(in_2), .Qn(j_k_ff_1_qn), .reset(in_3));  // open: Q, preset
  // Probe on j_k_ff_2_qn
  J_K_Flip_Flop #(.Pre_Clr_Positions("LEGACY"), .NewFFLayout("false")) j_k_ff_2 (
    .J(in_2), .clk(j_k_ff_3_q), .K(in_2), .Q(j_k_ff_2_q), .Qn(j_k_ff_2_qn), .reset(in_3));  // open: preset
  // Probe on j_k_ff_3_qn
  J_K_Flip_Flop #(.Pre_Clr_Positions("LEGACY"), .NewFFLayout("false")) j_k_ff_3 (
    .J(in_2), .clk(j_k_ff_4_q), .K(in_2), .Q(j_k_ff_3_q), .Qn(j_k_ff_3_qn), .reset(in_3));  // open: preset
  J_K_Flip_Flop #(.Pre_Clr_Positions("LEGACY"), .NewFFLayout("false")) j_k_ff_4 (
    .J(in_2), .clk(j_k_ff_5_q), .K(in_2), .Q(j_k_ff_4_q), .Qn(j_k_ff_4_qn), .reset(in_3));  // open: preset
  // Probe on j_k_ff_4_qn
  J_K_Flip_Flop #(.Pre_Clr_Positions("LEGACY"), .NewFFLayout("false")) j_k_ff_5 (
    .J(in_2), .clk(in_1), .K(in_2), .Q(j_k_ff_5_q), .Qn(j_k_ff_5_qn), .reset(in_3));  // open: preset
  // Probe on j_k_ff_5_qn
endmodule

module Guia_1303 (
  input  in_1,
  input  in_2,
  input  in_3
);

  wire j_k_ff_1_q, j_k_ff_1_qn, j_k_ff_2_q, j_k_ff_2_qn, j_k_ff_3_q, j_k_ff_3_qn, j_k_ff_4_q;

  // Probe on j_k_ff_4_q
  J_K_Flip_Flop #(.Pre_Clr_Positions("LEGACY"), .NewFFLayout("false")) j_k_ff_1 (
    .J(in_1), .clk(in_2), .K(in_1), .Q(j_k_ff_1_q), .Qn(j_k_ff_1_qn), .reset(in_3));  // open: preset
  // Probe on j_k_ff_3_q
  J_K_Flip_Flop #(.Pre_Clr_Positions("LEGACY"), .NewFFLayout("false")) j_k_ff_2 (
    .J(in_1), .clk(j_k_ff_1_qn), .K(in_1), .Q(j_k_ff_2_q), .Qn(j_k_ff_2_qn), .reset(in_3));  // open: preset
  // Probe on j_k_ff_2_q
  J_K_Flip_Flop #(.Pre_Clr_Positions("LEGACY"), .NewFFLayout("false")) j_k_ff_3 (
    .J(in_1), .clk(j_k_ff_2_qn), .K(in_1), .Q(j_k_ff_3_q), .Qn(j_k_ff_3_qn), .reset(in_3));  // open: preset
  // Probe on j_k_ff_1_q
  J_K_Flip_Flop #(.Pre_Clr_Positions("LEGACY"), .NewFFLayout("false")) j_k_ff_4 (
    .J(in_1), .clk(j_k_ff_3_qn), .K(in_1), .Q(j_k_ff_4_q), .reset(in_3));  // open: Qn, preset
endmodule

module Guia_1304 (
  input  in_1,
  input  in_2,
  input  in_3
);

  wire j_k_ff_1_q, j_k_ff_2_q, j_k_ff_3_q, j_k_ff_4_q;

  // Probe on j_k_ff_4_q
  J_K_Flip_Flop #(.Pre_Clr_Positions("LEGACY"), .NewFFLayout("false")) j_k_ff_1 (
    .J(in_1), .clk(in_2), .K(in_1), .Q(j_k_ff_1_q), .reset(in_3));  // open: Qn, preset
  // Probe on j_k_ff_3_q
  J_K_Flip_Flop #(.Pre_Clr_Positions("LEGACY"), .NewFFLayout("false")) j_k_ff_2 (
    .J(in_1), .clk(j_k_ff_1_q), .K(in_1), .Q(j_k_ff_2_q), .reset(in_3));  // open: Qn, preset
  // Probe on j_k_ff_2_q
  J_K_Flip_Flop #(.Pre_Clr_Positions("LEGACY"), .NewFFLayout("false")) j_k_ff_3 (
    .J(in_1), .clk(j_k_ff_2_q), .K(in_1), .Q(j_k_ff_3_q), .reset(in_3));  // open: Qn, preset
  // Probe on j_k_ff_1_q
  J_K_Flip_Flop #(.Pre_Clr_Positions("LEGACY"), .NewFFLayout("false")) j_k_ff_4 (
    .J(in_1), .clk(j_k_ff_3_q), .K(in_1), .Q(j_k_ff_4_q), .reset(in_3));  // open: Qn, preset
endmodule

module Guia_1305 (
  input  in_1,
  input  in_2,
  input  in_3
);

  wire and_1_out, and_2_out, or_1_out, t_ff_1_q, t_ff_2_q, t_ff_3_q;

  // Probe on t_ff_3_q
  T_Flip_Flop #(.Pre_Clr_Positions("LEGACY"), .NewFFLayout("false")) t_ff_1 (
    .clk(in_2), .T(in_1), .Q(t_ff_1_q), .reset(or_1_out));  // open: Qn, preset
  or or_1 (or_1_out, in_3, and_1_out);
  and and_1 (and_1_out, t_ff_3_q, t_ff_2_q, t_ff_1_q);
  // Probe on t_ff_2_q
  T_Flip_Flop #(.Pre_Clr_Positions("LEGACY"), .NewFFLayout("false")) t_ff_2 (
    .clk(in_2), .T(t_ff_1_q), .Q(t_ff_2_q), .reset(or_1_out));  // open: Qn, preset
  and and_2 (and_2_out, t_ff_2_q, t_ff_1_q);
  // Probe on t_ff_1_q
  T_Flip_Flop #(.Pre_Clr_Positions("LEGACY"), .NewFFLayout("false")) t_ff_3 (
    .clk(in_2), .T(and_2_out), .Q(t_ff_3_q), .reset(or_1_out));  // open: Qn, preset
endmodule
