// Logisim project Guia_14.circ as structural Verilog: 7 circuits, main circuit Guia_1401
module Guia_1401 (
  input  Data,
  input  CLR,
  input  LD
);

  wire clock_1_out, d_ff_1_q, d_ff_2_q, d_ff_3_q, d_ff_4_q, d_ff_5_q, d_ff_6_q;

  Clock clock_1 (.out(clock_1_out));
  // Probe on d_ff_1_q
  D_Flip_Flop #(.Pre_Clr_Positions("LEGACY"), .NewFFLayout("false")) d_ff_1 (
    .clk(clock_1_out), .D(d_ff_2_q), .Q(d_ff_1_q), .reset(CLR));  // open: Qn, preset
  // Probe on d_ff_2_q
  D_Flip_Flop #(.Pre_Clr_Positions("LEGACY"), .NewFFLayout("false")) d_ff_2 (
    .clk(clock_1_out), .D(d_ff_3_q), .Q(d_ff_2_q), .reset(CLR));  // open: Qn, preset
  // Probe on d_ff_3_q
  D_Flip_Flop #(.Pre_Clr_Positions("LEGACY"), .NewFFLayout("false")) d_ff_3 (
    .clk(clock_1_out), .D(d_ff_4_q), .Q(d_ff_3_q), .reset(CLR));  // open: Qn, preset
  // Probe on d_ff_4_q
  D_Flip_Flop #(.Pre_Clr_Positions("LEGACY"), .NewFFLayout("false")) d_ff_4 (
    .clk(clock_1_out), .D(d_ff_5_q), .Q(d_ff_4_q), .reset(CLR));  // open: Qn, preset
  // Probe on d_ff_5_q
  D_Flip_Flop #(.Pre_Clr_Positions("LEGACY"), .NewFFLayout("false")) d_ff_5 (
    .clk(clock_1_out), .D(d_ff_6_q), .Q(d_ff_5_q), .reset(CLR));  // open: Qn, preset
  // Probe on d_ff_6_q
  D_Flip_Flop #(.Pre_Clr_Positions("LEGACY"), .NewFFLayout("false")) d_ff_6 (
    .clk(clock_1_out), .D(Data), .Q(d_ff_6_q), .preset(LD), .reset(CLR));  // open: Qn
endmodule

module Guia_1402 (
  input  Data,
  input  CLR,
  input  LD
);

  wire clock_1_out, d_ff_1_q, d_ff_2_q, d_ff_3_q, d_ff_4_q, d_ff_5_q, d_ff_6_q;

  Clock clock_1 (.out(clock_1_out));
  // Probe on d_ff_1_q
  D_Flip_Flop #(.Pre_Clr_Positions("LEGACY"), .NewFFLayout("false")) d_ff_1 (
    .clk(clock_1_out), .D(d_ff_2_q), .Q(d_ff_1_q), .preset(LD), .reset(CLR));  // open: Qn
  // Probe on d_ff_2_q
  D_Flip_Flop #(.Pre_Clr_Positions("LEGACY"), .NewFFLayout("false")) d_ff_2 (
    .clk(clock_1_out), .D(d_ff_3_q), .Q(d_ff_2_q), .preset(LD), .reset(CLR));  // open: Qn
  // Probe on d_ff_3_q
  D_Flip_Flop #(.Pre_Clr_Positions("LEGACY"), .NewFFLayout("false")) d_ff_3 (
    .clk(clock_1_out), .D(d_ff_4_q), .Q(d_ff_3_q), .preset(LD), .reset(CLR));  // open: Qn
  // Probe on d_ff_4_q
  D_Flip_Flop #(.Pre_Clr_Positions("LEGACY"), .NewFFLayout("false")) d_ff_4 (
    .clk(clock_1_out), .D(d_ff_5_q), .Q(d_ff_4_q), .preset(LD), .reset(CLR));  // open: Qn
  // Probe on d_ff_5_q
  D_Flip_Flop #(.Pre_Clr_Positions("LEGACY"), .NewFFLayout("false")) d_ff_5 (
    .clk(clock_1_out), .D(d_ff_6_q), .Q(d_ff_5_q), .preset(LD), .reset(CLR));  // open: Qn
  // Probe on d_ff_6_q
  D_Flip_Flop #(.Pre_Clr_Positions("LEGACY"), .NewFFLayout("false")) d_ff_6 (
    .clk(clock_1_out), .D(Data), .Q(d_ff_6_q), .preset(LD), .reset(CLR));  // open: Qn
endmodule

module Guia_1403 (
  input  Data,
  input  CLR,
  input  LD
);

  wire clock_1_out, d_ff_1_q, d_ff_2_q, d_ff_3_q, d_ff_4_q, d_ff_5_q, d_ff_6_q, or_1_out;

  Clock clock_1 (.out(clock_1_out));
  or or_1 (or_1_out, Data, d_ff_6_q);
  // Probe on d_ff_1_q
  D_Flip_Flop #(.Pre_Clr_Positions("LEGACY"), .NewFFLayout("false")) d_ff_1 (
    .clk(clock_1_out), .D(or_1_out), .Q(d_ff_1_q), .reset(CLR));  // open: Qn, preset
  // Probe on d_ff_2_q
  D_Flip_Flop #(.Pre_Clr_Positions("LEGACY"), .NewFFLayout("false")) d_ff_2 (
    .clk(clock_1_out), .D(d_ff_1_q), .Q(d_ff_2_q), .reset(CLR));  // open: Qn, preset
  // Probe on d_ff_3_q
  D_Flip_Flop #(.Pre_Clr_Positions("LEGACY"), .NewFFLayout("false")) d_ff_3 (
    .clk(clock_1_out), .D(d_ff_2_q), .Q(d_ff_3_q), .reset(CLR));  // open: Qn, preset
  D_Flip_Flop #(.Pre_Clr_Positions("LEGACY"), .NewFFLayout("false")) d_ff_4 (
    .clk(clock_1_out), .D(d_ff_3_q), .Q(d_ff_4_q), .reset(CLR));  // open: Qn, preset
  // Probe on d_ff_4_q
  // Probe on d_ff_5_q
  D_Flip_Flop #(.Pre_Clr_Positions("LEGACY"), .NewFFLayout("false")) d_ff_5 (
    .clk(clock_1_out), .D(d_ff_4_q), .Q(d_ff_5_q), .reset(CLR));  // open: Qn, preset
  // Probe on d_ff_6_q
  D_Flip_Flop #(.Pre_Clr_Positions("LEGACY"), .NewFFLayout("false")) d_ff_6 (
    .clk(clock_1_out), .D(d_ff_5_q), .Q(d_ff_6_q), .preset(LD), .reset(CLR));  // open: Qn
endmodule

module Guia_1404 (
  input  CLR,
  input  LD
);

  wire clock_1_out, d_ff_1_q, d_ff_1_qn, d_ff_2_q, d_ff_3_q, d_ff_4_q, d_ff_5_q, d_ff_6_q;

  Clock clock_1 (.out(clock_1_out));
  // Probe on d_ff_1_q
  D_Flip_Flop #(.Pre_Clr_Positions("LEGACY"), .NewFFLayout("false")) d_ff_1 (
    .clk(clock_1_out), .D(d_ff_2_q), .Q(d_ff_1_q), .Qn(d_ff_1_qn), .reset(CLR));  // open: preset
  // Probe on d_ff_2_q
  D_Flip_Flop #(.Pre_Clr_Positions("LEGACY"), .NewFFLayout("false")) d_ff_2 (
    .clk(clock_1_out), .D(d_ff_3_q), .Q(d_ff_2_q), .reset(CLR));  // open: Qn, preset
  // Probe on d_ff_3_q
  D_Flip_Flop #(.Pre_Clr_Positions("LEGACY"), .NewFFLayout("false")) d_ff_3 (
    .clk(clock_1_out), .D(d_ff_4_q), .Q(d_ff_3_q), .reset(CLR));  // open: Qn, preset
  D_Flip_Flop #(.Pre_Clr_Positions("LEGACY"), .NewFFLayout("false")) d_ff_4 (
    .clk(clock_1_out), .D(d_ff_5_q), .Q(d_ff_4_q), .reset(CLR));  // open: Qn, preset
  // Probe on d_ff_4_q
  // Probe on d_ff_5_q
  D_Flip_Flop #(.Pre_Clr_Positions("LEGACY"), .NewFFLayout("false")) d_ff_5 (
    .clk(clock_1_out), .D(d_ff_6_q), .Q(d_ff_5_q), .reset(CLR));  // open: Qn, preset
  // Probe on d_ff_6_q
  D_Flip_Flop #(.Pre_Clr_Positions("LEGACY"), .NewFFLayout("false")) d_ff_6 (
    .clk(clock_1_out), .D(d_ff_1_qn), .Q(d_ff_6_q), .preset(LD), .reset(CLR));  // open: Qn
endmodule

module Guia_1405 (
  input  CLR,
  input  PRE,
  input  LD5,
  input  LD4,
  input  LD3,
  input  LD2,
  input  LD1,
  input  LD0
);

  wire and_1_out, and_2_out, and_3_out, and_4_out, and_5_out, and_6_out, clock_1_out, d_ff_1_q, d_ff_2_q,
       d_ff_3_q, d_ff_4_q, d_ff_5_q, d_ff_6_q;

  Clock clock_1 (.out(clock_1_out));
  D_Flip_Flop #(.Pre_Clr_Positions("LEGACY"), .NewFFLayout("false")) d_ff_1 (
    .clk(clock_1_out), .D(1'b0), .Q(d_ff_1_q), .preset(and_1_out), .reset(CLR));  // open: Qn
  and and_1 (and_1_out, PRE, LD5);
  // Probe on d_ff_1_q
  and and_2 (and_2_out, PRE, LD4);
  // Probe on d_ff_2_q
  D_Flip_Flop #(.Pre_Clr_Positions("LEGACY"), .NewFFLayout("false")) d_ff_2 (
    .clk(clock_1_out), .D(d_ff_1_q), .Q(d_ff_2_q), .preset(and_2_out), .reset(CLR));  // open: Qn
  // Probe on d_ff_3_q
  D_Flip_Flop #(.Pre_Clr_Positions("LEGACY"), .NewFFLayout("false")) d_ff_3 (
    .clk(clock_1_out), .D(d_ff_2_q), .Q(d_ff_3_q), .preset(and_3_out), .reset(CLR));  // open: Qn
  and and_3 (and_3_out, PRE, LD3);
  // Probe on d_ff_4_q
  D_Flip_Flop #(.Pre_Clr_Positions("LEGACY"), .NewFFLayout("false")) d_ff_4 (
    .clk(clock_1_out), .D(d_ff_3_q), .Q(d_ff_4_q), .preset(and_4_out), .reset(CLR));  // open: Qn
  and and_4 (and_4_out, PRE, LD2);
  D_Flip_Flop #(.Pre_Clr_Positions("LEGACY"), .NewFFLayout("false")) d_ff_5 (
    .clk(clock_1_out), .D(d_ff_4_q), .Q(d_ff_5_q), .preset(and_5_out), .reset(CLR));  // open: Qn
  and and_5 (and_5_out, PRE, LD1);
  // Probe on d_ff_5_q
  and and_6 (and_6_out, PRE, LD0);
  // Probe on d_ff_6_q
  D_Flip_Flop #(.Pre_Clr_Positions("LEGACY"), .NewFFLayout("false")) d_ff_6 (
    .clk(clock_1_out), .D(d_ff_5_q), .Q(d_ff_6_q), .preset(and_6_out), .reset(CLR));  // open: Qn
endmodule

module Guia_1406 (
  input  Data,
  input  CLR,
  input  LD
);

  wire clock_1_out, d_ff_1_q, d_ff_2_q, d_ff_3_q, d_ff_4_q, d_ff_5_q, or_1_out;

  Clock clock_1 (.out(clock_1_out));
  // Probe on d_ff_1_q
  D_Flip_Flop #(.Pre_Clr_Positions("LEGACY"), .NewFFLayout("false")) d_ff_1 (
    .clk(clock_1_out), .D(d_ff_2_q), .Q(d_ff_1_q), .preset(LD), .reset(CLR));  // open: Qn
  // Probe on d_ff_2_q
  D_Flip_Flop #(.Pre_Clr_Positions("LEGACY"), .NewFFLayout("false")) d_ff_2 (
    .clk(clock_1_out), .D(d_ff_3_q), .Q(d_ff_2_q), .preset(LD), .reset(CLR));  // open: Qn
  // Probe on d_ff_3_q
  D_Flip_Flop #(.Pre_Clr_Positions("LEGACY"), .NewFFLayout("false")) d_ff_3 (
    .clk(clock_1_out), .D(d_ff_4_q), .Q(d_ff_3_q), .preset(LD), .reset(CLR));  // open: Qn
  // Probe on d_ff_4_q
  D_Flip_Flop #(.Pre_Clr_Positions("LEGACY"), .NewFFLayout("false")) d_ff_4 (
    .clk(clock_1_out), .D(d_ff_5_q), .Q(d_ff_4_q), .preset(LD), .reset(CLR));  // open: Qn
  // Probe on d_ff_5_q
  D_Flip_Flop #(.Pre_Clr_Positions("LEGACY"), .NewFFLayout("false")) d_ff_5 (
    .clk(clock_1_out), .D(or_1_out), .Q(d_ff_5_q), .preset(LD), .reset(CLR));  // open: Qn
  or or_1 (or_1_out, Data, d_ff_1_q);
endmodule

module Guia_1407 (
  input  CLR,
  input  PRE,
  input  LD4,
  input  LD3,
  input  LD2,
  input  LD1,
  input  LD0
);

  wire and_1_out, and_2_out, and_3_out, and_4_out, and_5_out, clock_1_out, d_ff_1_q, d_ff_2_q, d_ff_3_q,
       d_ff_4_q, d_ff_5_q, d_ff_5_qn;

  Clock clock_1 (.out(clock_1_out));
  // Probe on d_ff_1_q
  D_Flip_Flop #(.Pre_Clr_Positions("LEGACY"), .NewFFLayout("false")) d_ff_1 (
    .clk(clock_1_out), .D(d_ff_5_qn), .Q(d_ff_1_q), .preset(and_1_out), .reset(CLR));  // open: Qn
  and and_1 (and_1_out, PRE, LD4);
  and and_2 (and_2_out, PRE, LD3);
  // Probe on d_ff_2_q
  D_Flip_Flop #(.Pre_Clr_Positions("LEGACY"), .NewFFLayout("false")) d_ff_2 (
    .clk(clock_1_out), .D(d_ff_1_q), .Q(d_ff_2_q), .preset(and_2_out), .reset(CLR));  // open: Qn
  and and_3 (and_3_out, PRE, LD2);
  // Probe on d_ff_3_q
  D_Flip_Flop #(.Pre_Clr_Positions("LEGACY"), .NewFFLayout("false")) d_ff_3 (
    .clk(clock_1_out), .D(d_ff_2_q), .Q(d_ff_3_q), .preset(and_3_out), .reset(CLR));  // open: Qn
  // Probe on d_ff_4_q
  D_Flip_Flop #(.Pre_Clr_Positions("LEGACY"), .NewFFLayout("false")) d_ff_4 (
    .clk(clock_1_out), .D(d_ff_3_q), .Q(d_ff_4_q), .preset(and_4_out), .reset(CLR));  // open: Qn
  and and_4 (and_4_out, PRE, LD1);
  // Probe on d_ff_5_q
  D_Flip_Flop #(.Pre_Clr_Positions("LEGACY"), .NewFFLayout("false")) d_ff_5 (
    .clk(clock_1_out), .D(d_ff_4_q), .Q(d_ff_5_q), .Qn(d_ff_5_qn), .preset(and_5_out), .reset(CLR));
  and and_5 (and_5_out, PRE, LD0);
endmodule
