// Logisim project Guia_17.circ as structural Verilog: 5 circuits, main circuit 1
module _1 (
  input  a,
  input  b,
  input  c,
  output out_4,
  output out_5
);

  wire and_1_out, and_2_out, and_3_out, clock_1_out, not_1_out, not_2_out, or_1_out, or_2_out;

  not not_1 (not_1_out, c);
  not not_2 (not_2_out, a);
  Clock clock_1 (.out(clock_1_out));
  and and_1 (and_1_out, a, not_1_out);
  or or_1 (or_1_out, and_1_out, and_2_out);
  and and_2 (and_2_out, b, c);
  and and_3 (and_3_out, not_2_out, c);
  or or_2 (or_2_out, and_3_out, b);
  D_Flip_Flop #(.Pre_Clr_Positions("LEGACY"), .NewFFLayout("false")) d_ff_1 (
    .clk(clock_1_out), .D(or_1_out), .Q(out_4));  // open: Qn, preset, reset
  D_Flip_Flop #(.Pre_Clr_Positions("LEGACY"), .NewFFLayout("false")) d_ff_2 (
    .clk(clock_1_out), .D(or_2_out), .Q(out_5));  // open: Qn, preset, reset
endmodule

module _2 (
  input  in_1,
  input  in_2,
  input  in_3,
  output out_4,
  output out_5
);

  wire and_1_out, and_2_out, and_3_out, and_4_out, and_5_out, and_6_out, and_7_out, and_8_out, clock_1_out,
       not_1_out, not_2_out, not_3_out, not_4_out, not_5_out, not_6_out, not_7_out, not_8_out, or_1_out,
       or_2_out, or_3_out, or_4_out;

  not not_1 (not_1_out, in_3);
  not not_2 (not_2_out, in_1);
  not not_3 (not_3_out, in_3);
  not not_4 (not_4_out, in_2);
  not not_5 (not_5_out, in_1);
  not not_6 (not_6_out, in_3);
  not not_7 (not_7_out, in_2);
  not not_8 (not_8_out, in_3);
  Clock clock_1 (.out(clock_1_out));
  and and_1 (and_1_out, in_1, not_1_out);
  or or_1 (or_1_out, and_1_out, and_2_out);
  and and_2 (and_2_out, in_2, in_3);
  and and_3 (and_3_out, not_2_out, not_3_out);
  or or_2 (or_2_out, and_3_out, and_4_out);
  and and_4 (and_4_out, not_4_out, in_3);
  and and_5 (and_5_out, not_5_out, in_3);
  or or_3 (or_3_out, and_5_out, and_6_out);
  and and_6 (and_6_out, in_2, not_6_out);
  and and_7 (and_7_out, in_1, in_3);
  or or_4 (or_4_out, and_7_out, and_8_out);
  and and_8 (and_8_out, not_7_out, not_8_out);
  J_K_Flip_Flop #(.Pre_Clr_Positions("LEGACY"), .NewFFLayout("false")) j_k_ff_1 (
    .J(or_1_out), .clk(clock_1_out), .K(or_2_out), .Q(out_4));  // open: Qn, preset, reset
  J_K_Flip_Flop #(.Pre_Clr_Positions("LEGACY"), .NewFFLayout("false")) j_k_ff_2 (
    .J(or_3_out), .clk(clock_1_out), .K(or_4_out), .Q(out_5));  // open: Qn, preset, reset
endmodule

module _3 (
  input  in_1,
  input  in_2,
  input  in_3,
  output out_4,
  output out_5
);

  wire and_1_out, and_2_out, and_3_out, and_4_out, clock_1_out, not_1_out, not_2_out, not_3_out, not_4_out,
       or_1_out, or_2_out;

  not not_1 (not_1_out, in_1);
  not not_2 (not_2_out, in_2);
  not not_3 (not_3_out, in_1);
  not not_4 (not_4_out, in_2);
  Clock clock_1 (.out(clock_1_out));
  and and_1 (and_1_out, not_1_out, in_2, in_3);
  or or_1 (or_1_out, and_1_out, and_2_out);
  and and_2 (and_2_out, in_1, not_2_out, in_3);
  and and_3 (and_3_out, not_3_out, not_4_out, in_3);
  or or_2 (or_2_out, and_3_out, and_4_out);
  and and_4 (and_4_out, in_1, in_2, in_3);
  J_K_Flip_Flop #(.Pre_Clr_Positions("LEGACY"), .NewFFLayout("false")) j_k_ff_1 (
    .J(or_1_out), .clk(clock_1_out), .K(or_1_out), .Q(out_4));  // open: Qn, preset, reset
  J_K_Flip_Flop #(.Pre_Clr_Positions("LEGACY"), .NewFFLayout("false")) j_k_ff_2 (
    .J(or_2_out), .clk(clock_1_out), .K(or_2_out), .Q(out_5));  // open: Qn, preset, reset
endmodule

module _4 (
  input  in_1,
  output [2:0] out_2
);

  wire clock_1_out;

  Clock clock_1 (.out(clock_1_out));
  T_Flip_Flop #(.Pre_Clr_Positions("LEGACY"), .NewFFLayout("false")) t_ff_1 (
    .clk(clock_1_out), .T(1'b1), .Q(out_2[0]), .reset(in_1));  // open: Qn, preset
  T_Flip_Flop #(.Pre_Clr_Positions("LEGACY"), .NewFFLayout("false")) t_ff_2 (
    .clk(out_2[0]), .T(1'b1), .Q(out_2[1]), .reset(in_1));  // open: Qn, preset
  T_Flip_Flop #(.Pre_Clr_Positions("LEGACY"), .NewFFLayout("false")) t_ff_3 (
    .clk(out_2[1]), .T(1'b1), .Q(out_2[2]), .reset(in_1));  // open: Qn, preset
endmodule

module _5 (
  input  in_1,
  output [2:0] out_2
);

  wire clock_1_out, t_ff_1_qn, t_ff_2_qn;

  Clock clock_1 (.out(clock_1_out));
  T_Flip_Flop #(.Pre_Clr_Positions("LEGACY"), .NewFFLayout("false")) t_ff_1 (
    .clk(clock_1_out), .T(1'b1), .Q(out_2[0]), .Qn(t_ff_1_qn), .reset(in_1));  // open: preset
  T_Flip_Flop #(.Pre_Clr_Positions("LEGACY"), .NewFFLayout("false")) t_ff_2 (
    .clk(t_ff_1_qn), .T(1'b1), .Q(out_2[1]), .Qn(t_ff_2_qn), .reset(in_1));  // open: preset
  T_Flip_Flop #(.Pre_Clr_Positions("LEGACY"), .NewFFLayout("false")) t_ff_3 (
    .clk(t_ff_2_qn), .T(1'b1), .Q(out_2[2]), .reset(in_1));  // open: Qn, preset
endmodule
