// Logisim project R_0101a.circ as structural Verilog: 1 circuit, main circuit main
module main (
  input  a,
  input  b,
  input  c,
  input  d
);

  wire and_1_out, and_2_out, and_3_out, and_4_out, and_5_out, and_6_out, not_1_out, not_2_out, not_3_out,
       not_4_out;

  not not_1 (not_1_out, a);
  not not_2 (not_2_out, b);
  not not_3 (not_3_out, c);
  not not_4 (not_4_out, d);
  and and_1 (and_1_out, not_1_out, b, not_3_out, not_4_out);
  and and_2 (and_2_out, a, not_2_out, not_3_out, not_4_out);
  and and_3 (and_3_out, a, not_2_out, not_3_out, d);
  and and_4 (and_4_out, a, b, not_3_out, not_4_out);
  and and_5 (and_5_out, a, b, not_3_out, d);
  and and_6 (and_6_out, a, b, c, not_4_out);
  // OR_Gate or_1 has open pins: in0=and_1_out, in1=and_2_out, in2=and_3_out, in3=and_4_out, in4=and_5_out, in5=and_6_out, out=open
endmodule
