// Logisim project R_0101b.circ as structural Verilog: 1 circuit, main circuit main
module main (
  input  a,
  input  b,
  input  c,
  input  d,
  output s
);

  wire not_1_out, not_2_out, not_3_out, not_4_out, or_1_out, or_2_out, or_3_out, or_4_out, or_5_out,
       or_6_out, or_7_out, or_8_out, or_9_out, or_10_out;

  not not_1 (not_1_out, a);
  not not_2 (not_2_out, c);
  not not_3 (not_3_out, b);
  not not_4 (not_4_out, d);
  or or_1 (or_1_out, a, b, c, d);
  or or_2 (or_2_out, a, b, c, not_4_out);
  or or_3 (or_3_out, a, b, not_2_out, d);
  or or_4 (or_4_out, a, b, not_2_out, not_4_out);
  or or_5 (or_5_out, a, not_3_out, c, not_4_out);
  or or_6 (or_6_out, a, not_3_out, not_2_out, d);
  or or_7 (or_7_out, a, not_3_out, not_2_out, not_4_out);
  or or_8 (or_8_out, not_1_out, b, not_2_out, d);
  or or_9 (or_9_out, not_1_out, b, not_2_out, not_4_out);
  or or_10 (or_10_out, not_1_out, not_3_out, not_2_out, not_4_out);
  and and_1 (s, or_1_out, or_2_out, or_3_out, or_4_out, or_5_out, or_6_out, or_7_out, or_8_out, or_9_out, or_10_out);
endmodule
