// Logisim project R_0101d.circ as structural Verilog: 1 circuit, main circuit main
module main (
  input  a,
  input  b,
  input  c,
  input  d,
  output s
);

  wire not_1_out, not_2_out, not_3_out, not_4_out, or_1_out, or_2_out, or_3_out, or_4_out, or_5_out;

  not not_1 (not_1_out, a);
  not not_2 (not_2_out, c);
  not not_3 (not_3_out, d);
  not not_4 (not_4_out, b);
  or or_1 (or_1_out, a, b);
  or or_2 (or_2_out, a, not_3_out);
  or or_3 (or_3_out, a, not_2_out);
  or or_4 (or_4_out, b, not_2_out);
  or or_5 (or_5_out, not_2_out, not_3_out);
  and and_1 (s, or_1_out, or_2_out, or_3_out, or_4_out, or_5_out);
endmodule
