// Logisim project R_0102a.circ as structural Verilog: 1 circuit, main circuit main
module main (
  input  a,
  input  c,
  output s
);

  wire not_1_out;

  not not_1 (not_1_out, a);
  Multiplexer #(.enable("false")) multiplexer_1 (.in0(not_1_out), .in1(c), .out(s), .sel(a));
endmodule
