// Logisim project R_0102b.circ as structural Verilog: 1 circuit, main circuit main
module main (
  input  a,
  input  b,
  input  c,
  output s
);

  wire multiplexer_1_out, not_1_out, not_2_out;

  not not_1 (not_1_out, a);
  Multiplexer #(.enable("false")) multiplexer_1 (.in0(not_1_out), .in1(b), .out(multiplexer_1_out), .sel(a));
  not not_2 (not_2_out, c);
  Multiplexer #(.enable("false")) multiplexer_2 (.in0(not_2_out), .in1(multiplexer_1_out), .out(s), .sel(c));
endmodule
