// Logisim project R_0103b.circ as structural Verilog: 1 circuit, main circuit main
module main (
  input  a,
  input  b,
  output s
);

  wire nand_1_out, nand_2_out, not_1_out, not_2_out, not_3_out;

  not not_1 (not_1_out, a);
  not not_2 (not_2_out, a);
  not not_3 (not_3_out, b);
  nand nand_1 (nand_1_out, not_1_out, b);
  and and_1 (s, nand_1_out, nand_2_out);
  nand nand_2 (nand_2_out, not_2_out, not_3_out);
endmodule
