// Logisim project Recuperacao_02.circ as structural Verilog: 9 circuits, main circuit 3
module _3 (
  input  in_1,
  output [2:0] out_2
);

  wire clock_1_out;

  Clock clock_1 (.out(clock_1_out));
  J_K_Flip_Flop #(.Pre_Clr_Positions("LEGACY"), .NewFFLayout("false")) j_k_ff_1 (
    .J(1'b1), .clk(clock_1_out), .K(1'b1), .Q(out_2[0]), .reset(in_1));  // open: Qn, preset
  J_K_Flip_Flop #(.Pre_Clr_Positions("LEGACY"), .NewFFLayout("false")) j_k_ff_2 (
    .J(out_2[0]), .clk(clock_1_out), .K(out_2[0]), .Q(out_2[1]), .reset(in_1));  // open: Qn, preset
  J_K_Flip_Flop #(.Pre_Clr_Positions("LEGACY"), .NewFFLayout("false")) j_k_ff_3 (
    .J(out_2[1]), .clk(clock_1_out), .K(out_2[1]), .Q(out_2[2]), .reset(in_1));  // open: Qn, preset
endmodule

module _4 (
  input  in_1,
  output [2:0] out_2
);

  wire clock_1_out, d_ff_2_qn;

  Clock clock_1 (.out(clock_1_out));
  D_Flip_Flop #(.Pre_Clr_Positions("LEGACY"), .NewFFLayout("false")) d_ff_1 (
    .clk(clock_1_out), .D(1'b1), .Q(out_2[0]), .reset(in_1));  // open: Qn, preset
  D_Flip_Flop #(.Pre_Clr_Positions("LEGACY"), .NewFFLayout("false")) d_ff_2 (
    .clk(clock_1_out), .D(out_2[0]), .Q(out_2[1]), .Qn(d_ff_2_qn), .reset(in_1));  // open: preset
  D_Flip_Flop #(.Pre_Clr_Positions("LEGACY"), .NewFFLayout("false")) d_ff_3 (
    .clk(clock_1_out), .D(d_ff_2_qn), .Q(out_2[2]), .reset(in_1));  // open: Qn, preset
endmodule

module _5 (
  input  in_1,
  output [3:0] out_2
);

  wire and_1_out, clock_1_out, or_1_out, t_ff_1_qn, t_ff_2_qn, t_ff_3_qn;

  or or_1 (or_1_out, in_1, and_1_out);
  and and_1 (and_1_out, t_ff_1_qn, out_2[1], t_ff_3_qn, out_2[3]);
  T_Flip_Flop #(.Pre_Clr_Positions("LEGACY"), .NewFFLayout("false")) t_ff_1 (
    .clk(clock_1_out), .T(1'b1), .Q(out_2[0]), .Qn(t_ff_1_qn), .reset(or_1_out));  // open: preset
  Clock clock_1 (.out(clock_1_out));
  T_Flip_Flop #(.Pre_Clr_Positions("LEGACY"), .NewFFLayout("false")) t_ff_2 (
    .clk(t_ff_1_qn), .T(1'b1), .Q(out_2[1]), .Qn(t_ff_2_qn), .reset(or_1_out));  // open: preset
  T_Flip_Flop #(.Pre_Clr_Positions("LEGACY"), .NewFFLayout("false")) t_ff_3 (
    .clk(t_ff_2_qn), .T(1'b1), .Q(out_2[2]), .Qn(t_ff_3_qn), .reset(or_1_out));  // open: preset
  T_Flip_Flop #(.Pre_Clr_Positions("LEGACY"), .NewFFLayout("false")) t_ff_4 (
    .clk(t_ff_3_qn), .T(1'b1), .Q(out_2[3]), .reset(or_1_out));  // open: Qn, preset
endmodule

module _1a (
  input  a,
  input  b,
  input  c,
  input  d,
  output s
);

  wire and_1_out, and_2_out, and_3_out, and_4_out, not_1_out, not_2_out, not_3_out, not_4_out;

  not not_1 (not_1_out, a);
  not not_2 (not_2_out, c);
  not not_3 (not_3_out, b);
  not not_4 (not_4_out, d);
  and and_1 (and_1_out, not_1_out, b, c, d);
  and and_2 (and_2_out, a, not_2_out, d);
  and and_3 (and_3_out, a, c, not_4_out);
  and and_4 (and_4_out, a, not_3_out, d);
  or or_1 (s, and_1_out, and_2_out, and_3_out, and_4_out);
endmodule

module _1b (
  input  a,
  input  b,
  input  c,
  input  d,
  output s
);

  wire not_2_out, not_3_out, not_4_out, or_1_out, or_2_out, or_3_out, or_4_out;

  // NOT_Gate not_1 has open pins: in=a, out=open
  not not_2 (not_2_out, b);
  not not_3 (not_3_out, c);
  not not_4 (not_4_out, d);
  or or_1 (or_1_out, not_2_out, not_3_out, not_4_out);
  or or_2 (or_2_out, c, d);
  or or_3 (or_3_out, b, c);
  or or_4 (or_4_out, b, d);
  and and_1 (s, or_1_out, or_2_out, or_3_out, or_4_out);
endmodule

module _1c (
  input  a,
  input  b,
  input  c,
  input  d,
  output s
);

  wire and_1_out, and_2_out, and_3_out, and_4_out, not_1_out, not_2_out, not_3_out, not_4_out;

  not not_1 (not_1_out, a);
  not not_2 (not_2_out, c);
  not not_3 (not_3_out, b);
  not not_4 (not_4_out, d);
  and and_1 (and_1_out, not_2_out, d);
  and and_2 (and_2_out, c, not_4_out);
  and and_3 (and_3_out, not_1_out, d);
  and and_4 (and_4_out, not_3_out, d);
  or or_1 (s, and_1_out, and_2_out, and_3_out, and_4_out);
endmodule

module _1d (
  input  a,
  input  b,
  input  c,
  input  d,
  output s
);

  wire and_1_out, and_2_out, not_3_out, not_4_out;

  // NOT_Gate not_1 has open pins: in=a, out=open
  // NOT_Gate not_2 has open pins: in=b, out=open
  not not_3 (not_3_out, c);
  not not_4 (not_4_out, d);
  and and_1 (and_1_out, a, not_3_out, not_4_out);
  and and_2 (and_2_out, b, c, d);
  or or_1 (s, and_1_out, and_2_out);
endmodule

module _1e (
  input  a,
  input  b,
  input  c,
  input  d,
  output s
);

  wire not_3_out, not_4_out, or_1_out, or_2_out, or_3_out;

  // NOT_Gate not_1 has open pins: in=a, out=open
  // NOT_Gate not_2 has open pins: in=b, out=open
  not not_3 (not_3_out, c);
  not not_4 (not_4_out, d);
  or or_1 (or_1_out, c, not_4_out);
  or or_2 (or_2_out, not_3_out, d);
  or or_3 (or_3_out, b, c);
  and and_1 (s, or_1_out, or_2_out, or_3_out);
endmodule

module _1f (
  input  a,
  input  b,
  input  c,
  input  d,
  output s
);

  wire and_1_out, and_2_out, not_3_out;

  // NOT_Gate not_1 has open pins: in=a, out=open
  // NOT_Gate not_2 has open pins: in=b, out=open
  not not_3 (not_3_out, c);
  // NOT_Gate not_4 has open pins: in=d, out=open
  and and_1 (and_1_out, a, b, d);
  and and_2 (and_2_out, not_3_out, d);
  or or_1 (s, and_1_out, and_2_out);
endmodule
