// Logisim project additive-circuits.circ as structural Verilog: 4 circuits, main circuit half-adder
module half_adder (
  input  b,
  input  a,
  output s0,
  output s1
);

  xor xor_1 (s0, b, a);
  and and_1 (s1, b, a);
endmodule

module full_adder (
  input  c,
  input  b,
  input  a,
  output s0,
  output s1
);

  wire HA_2_s0, HA_2_s1, HA_s1;

  half_adder HA (.b(c), .a(HA_2_s0), .s0(s0), .s1(HA_s1));
  half_adder HA_2 (.b(b), .a(a), .s0(HA_2_s0), .s1(HA_2_s1));
  or or_1 (s1, HA_s1, HA_2_s1);
endmodule

module byte_sum (
  input  [7:0] in_1,
  input  [7:0] in_2,
  output [7:0] out_3
);

  wire FA_2_s1, FA_3_s1, FA_4_s1, FA_5_s1, FA_6_s1, FA_7_s1, FA_s1;

  full_adder FA (.c(1'b0), .b(in_2[0]), .a(in_1[0]), .s1(FA_s1));  // open: s0
  full_adder FA_2 (.c(FA_s1), .b(in_2[1]), .a(in_1[1]), .s1(FA_2_s1));  // open: s0
  full_adder FA_3 (.c(FA_2_s1), .b(in_2[2]), .a(in_1[2]), .s1(FA_3_s1));  // open: s0
  full_adder FA_4 (.c(FA_3_s1), .b(in_2[3]), .a(in_1[3]), .s1(FA_4_s1));  // open: s0
  full_adder FA_5 (.c(FA_4_s1), .b(in_2[4]), .a(in_1[4]), .s1(FA_5_s1));  // open: s0
  full_adder FA_6 (.c(FA_5_s1), .b(in_2[5]), .a(in_1[5]), .s1(FA_6_s1));  // open: s0
  full_adder FA_7 (.c(FA_6_s1), .b(in_2[6]), .a(in_1[6]), .s1(FA_7_s1));  // open: s0
  full_adder FA_8 (.c(FA_7_s1), .b(in_2[7]), .a(in_1[7]));  // open: s0, s1
endmodule

module complete_circuit (
  input  [7:0] in_1,
  input  [7:0] in_2,
  output [7:0] out_3
);

  wire and_1_out, and_2_out, and_3_out, and_4_out, and_5_out, and_6_out, and_7_out, and_8_out, and_9_out,
       and_10_out, and_11_out, and_12_out, and_13_out, and_14_out, and_15_out, and_16_out, or_1_out,
       or_2_out, or_3_out, or_4_out, or_5_out, or_6_out, or_7_out, xor_1_out, xor_2_out, xor_3_out,
       xor_4_out, xor_5_out, xor_6_out, xor_7_out, xor_8_out;

  xor xor_1 (xor_1_out, in_1[0], in_2[0]);
  xor xor_2 (xor_2_out, in_1[1], in_2[1]);
  xor xor_3 (xor_3_out, in_1[2], in_2[2]);
  xor xor_4 (xor_4_out, in_1[3], in_2[3]);
  xor xor_5 (xor_5_out, in_1[4], in_2[4]);
  xor xor_6 (xor_6_out, in_1[5], in_2[5]);
  xor xor_7 (xor_7_out, in_1[6], in_2[6]);
  xor xor_8 (xor_8_out, in_1[7], in_2[7]);
  xor xor_9 (out_3[0], xor_1_out, 1'b0);
  and and_1 (and_1_out, in_1[0], in_2[0]);
  and and_2 (and_2_out, 1'b0, xor_1_out);
  xor xor_10 (out_3[1], xor_2_out, or_1_out);
  and and_3 (and_3_out, in_1[1], in_2[1]);
  and and_4 (and_4_out, or_1_out, xor_2_out);
  xor xor_11 (out_3[2], xor_3_out, or_2_out);
  and and_5 (and_5_out, in_1[2], in_2[2]);
  and and_6 (and_6_out, or_2_out, xor_3_out);
  xor xor_12 (out_3[3], xor_4_out, or_3_out);
  and and_7 (and_7_out, in_1[3], in_2[3]);
  and and_8 (and_8_out, or_3_out, xor_4_out);
  xor xor_13 (out_3[4], xor_5_out, or_4_out);
  and and_9 (and_9_out, in_1[4], in_2[4]);
  and and_10 (and_10_out, or_4_out, xor_5_out);
  xor xor_14 (out_3[5], xor_6_out, or_5_out);
  and and_11 (and_11_out, in_1[5], in_2[5]);
  and and_12 (and_12_out, or_5_out, xor_6_out);
  xor xor_15 (out_3[6], xor_7_out, or_6_out);
  and and_13 (and_13_out, in_1[6], in_2[6]);
  and and_14 (and_14_out, or_6_out, xor_7_out);
  xor xor_16 (out_3[7], xor_8_out, or_7_out);
  and and_15 (and_15_out, in_1[7], in_2[7]);
  and and_16 (and_16_out, or_7_out, xor_8_out);
  or or_1 (or_1_out, and_1_out, and_2_out);
  or or_2 (or_2_out, and_3_out, and_4_out);
  or or_3 (or_3_out, and_5_out, and_6_out);
  or or_4 (or_4_out, and_7_out, and_8_out);
  or or_5 (or_5_out, and_9_out, and_10_out);
  or or_6 (or_6_out, and_11_out, and_12_out);
  or or_7 (or_7_out, and_13_out, and_14_out);
  // OR_Gate or_8 has open pins: in0=and_15_out, in1=and_16_out, out=open
endmodule
