// Logisim project bit-shifting.circ as structural Verilog: 2 circuits, main circuit rbs
module rbs (
  input  in_1,
  input  in_2,
  input  in_3,
  input  in_4,
  input  in_5,
  output [3:0] out_6
);

  wire button_1_out;

  Button button_1 (.out(button_1_out));
  D_Flip_Flop #(.Pre_Clr_Positions("LEGACY"), .NewFFLayout("false")) d_ff_1 (
    .clk(button_1_out), .D(1'b0), .Q(out_6[3]), .preset(in_1), .reset(in_5));  // open: Qn
  D_Flip_Flop #(.Pre_Clr_Positions("LEGACY"), .NewFFLayout("false")) d_ff_2 (
    .clk(button_1_out), .D(out_6[3]), .Q(out_6[2]), .preset(in_2), .reset(in_5));  // open: Qn
  D_Flip_Flop #(.Pre_Clr_Positions("LEGACY"), .NewFFLayout("false")) d_ff_3 (
    .clk(button_1_out), .D(out_6[2]), .Q(out_6[1]), .preset(in_3), .reset(in_5));  // open: Qn
  D_Flip_Flop #(.Pre_Clr_Positions("LEGACY"), .NewFFLayout("false")) d_ff_4 (
    .clk(button_1_out), .D(out_6[1]), .Q(out_6[0]), .preset(in_4), .reset(in_5));  // open: Qn
endmodule

module lbs (
  input  in_1,
  input  in_2,
  input  in_3,
  input  in_4,
  input  in_5,
  output [3:0] out_6
);

  wire button_1_out;

  Button button_1 (.out(button_1_out));
  D_Flip_Flop #(.Pre_Clr_Positions("LEGACY"), .NewFFLayout("false")) d_ff_1 (
    .clk(button_1_out), .D(out_6[2]), .Q(out_6[3]), .preset(in_1), .reset(in_5));  // open: Qn
  D_Flip_Flop #(.Pre_Clr_Positions("LEGACY"), .NewFFLayout("false")) d_ff_2 (
    .clk(button_1_out), .D(out_6[1]), .Q(out_6[2]), .preset(in_2), .reset(in_5));  // open: Qn
  D_Flip_Flop #(.Pre_Clr_Positions("LEGACY"), .NewFFLayout("false")) d_ff_3 (
    .clk(button_1_out), .D(out_6[0]), .Q(out_6[1]), .preset(in_3), .reset(in_5));  // open: Qn
  D_Flip_Flop #(.Pre_Clr_Positions("LEGACY"), .NewFFLayout("false")) d_ff_4 (
    .clk(button_1_out), .D(1'b0), .Q(out_6[0]), .preset(in_4), .reset(in_5));  // open: Qn
endmodule
