// Logisim project counters.circ as structural Verilog: 2 circuits, main circuit ascending-counter
module ascending_counter (
  input  in_1,
  input  in_2
);

  wire and_1_out, and_2_out, and_3_out, and_4_out, and_5_out, clock_1_out, j_k_ff_1_q, j_k_ff_2_q, not_1_out,
       not_2_out, not_3_out, not_4_out, not_5_out, not_6_out, not_7_out, or_1_out, or_2_out;

  Clock clock_1 (.out(clock_1_out));
  not not_1 (not_1_out, in_1);
  and and_1 (and_1_out, not_1_out, j_k_ff_1_q);
  and and_2 (and_2_out, j_k_ff_1_q, not_2_out);
  not not_2 (not_2_out, j_k_ff_2_q);
  and and_3 (and_3_out, in_1, j_k_ff_2_q, not_3_out);
  not not_3 (not_3_out, j_k_ff_1_q);
  not not_4 (not_4_out, in_1);
  and and_4 (and_4_out, not_4_out, j_k_ff_2_q);
  and and_5 (and_5_out, in_1, not_5_out);
  not not_5 (not_5_out, j_k_ff_2_q);
  or or_1 (or_1_out, and_1_out, and_2_out, and_3_out);
  not not_6 (not_6_out, or_1_out);
  or or_2 (or_2_out, and_4_out, and_5_out);
  not not_7 (not_7_out, or_2_out);
  J_K_Flip_Flop #(.Pre_Clr_Positions("LEGACY"), .NewFFLayout("false")) j_k_ff_1 (
    .J(or_1_out), .clk(clock_1_out), .K(not_6_out), .Q(j_k_ff_1_q), .reset(in_2));  // open: Qn, preset
  J_K_Flip_Flop #(.Pre_Clr_Positions("LEGACY"), .NewFFLayout("false")) j_k_ff_2 (
    .J(or_2_out), .clk(clock_1_out), .K(not_7_out), .Q(j_k_ff_2_q), .reset(in_2));  // open: Qn, preset
endmodule

module descending_counter (
  input  in_1,
  input  in_2
);

  wire and_1_out, and_2_out, and_3_out, and_4_out, and_5_out, clock_1_out, j_k_ff_1_q, j_k_ff_2_q, not_1_out,
       not_2_out, not_3_out, not_4_out, not_5_out, not_6_out, not_7_out, or_1_out, or_2_out;

  Clock clock_1 (.out(clock_1_out));
  and and_1 (and_1_out, j_k_ff_1_q, not_1_out);
  not not_1 (not_1_out, in_1);
  and and_2 (and_2_out, j_k_ff_1_q, j_k_ff_2_q);
  not not_2 (not_2_out, j_k_ff_1_q);
  and and_3 (and_3_out, not_2_out, in_1, not_3_out);
  not not_3 (not_3_out, j_k_ff_2_q);
  and and_4 (and_4_out, j_k_ff_2_q, not_4_out);
  not not_4 (not_4_out, in_1);
  not not_5 (not_5_out, j_k_ff_2_q);
  and and_5 (and_5_out, not_5_out, in_1);
  or or_1 (or_1_out, and_1_out, and_2_out, and_3_out);
  not not_6 (not_6_out, or_1_out);
  or or_2 (or_2_out, and_4_out, and_5_out);
  not not_7 (not_7_out, or_2_out);
  J_K_Flip_Flop #(.Pre_Clr_Positions("LEGACY"), .NewFFLayout("false")) j_k_ff_1 (
    .J(or_1_out), .clk(clock_1_out), .K(not_6_out), .Q(j_k_ff_1_q), .reset(in_2));  // open: Qn, preset
  J_K_Flip_Flop #(.Pre_Clr_Positions("LEGACY"), .NewFFLayout("false")) j_k_ff_2 (
    .J(or_2_out), .clk(clock_1_out), .K(not_7_out), .Q(j_k_ff_2_q), .reset(in_2));  // open: Qn, preset
endmodule
