// Logisim project frequency-division.circ as structural Verilog: 2 circuits, main circuit division_by_3
module division_by_3 (
  input  in_1,
  input  in_2,
  input  in_3,
  output out_4
);

  wire clock_1_out, d_ff_1_q, d_ff_2_qn, digital_oscilloscope_1_p3, nand_1_out, nand_3_out;

  Clock clock_1 (.out(clock_1_out));
  nand nand_1 (nand_1_out, digital_oscilloscope_1_p3, d_ff_1_q);
  D_Flip_Flop #(.Pre_Clr_Positions("LEGACY"), .NewFFLayout("false")) d_ff_1 (
    .clk(clock_1_out), .D(nand_1_out), .Q(d_ff_1_q), .reset(in_1));  // open: Qn, preset
  // Digital_Oscilloscope digital_oscilloscope_1: pin names not known; wires that end beside it: clock_1_out, d_ff_1_q, digital_oscilloscope_1_p3, out_4, in_2, in_3
  D_Flip_Flop #(.Pre_Clr_Positions("LEGACY"), .NewFFLayout("false")) d_ff_2 (
    .clk(clock_1_out), .D(d_ff_1_q), .Q(digital_oscilloscope_1_p3), .Qn(d_ff_2_qn), .reset(in_1));  // open: preset
  nand nand_2 (out_4, d_ff_1_q, nand_3_out);
  nand nand_3 (nand_3_out, clock_1_out, d_ff_2_qn);
endmodule

module division_by_5 (
  input  in_1,
  input  in_2,
  input  in_3
);

  wire clock_1_out, d_ff_1_q, d_ff_1_qn, d_ff_2_q, d_ff_2_qn, d_ff_3_q, d_ff_4_q, digital_oscilloscope_1_p4,
       nand_1_out, nand_2_out, nand_3_out;

  Clock clock_1 (.out(clock_1_out));
  D_Flip_Flop #(.Pre_Clr_Positions("LEGACY"), .NewFFLayout("false")) d_ff_1 (
    .clk(clock_1_out), .D(nand_1_out), .Q(d_ff_1_q), .Qn(d_ff_1_qn), .reset(in_1));  // open: preset
  nand nand_1 (nand_1_out, d_ff_2_q, d_ff_3_q);
  D_Flip_Flop #(.Pre_Clr_Positions("LEGACY"), .NewFFLayout("false")) d_ff_2 (
    .clk(clock_1_out), .D(d_ff_1_q), .Q(d_ff_2_q), .Qn(d_ff_2_qn), .reset(in_1));  // open: preset
  // Digital_Oscilloscope digital_oscilloscope_1: pin names not known; wires that end beside it: clock_1_out, d_ff_1_q, d_ff_2_q, digital_oscilloscope_1_p4, in_2, in_3
  D_Flip_Flop #(.Pre_Clr_Positions("LEGACY"), .NewFFLayout("false")) d_ff_3 (
    .clk(clock_1_out), .D(d_ff_2_q), .Q(d_ff_3_q), .reset(in_1));  // open: Qn, preset
  nand nand_2 (nand_2_out, clock_1_out, clock_1_out);
  nand nand_3 (nand_3_out, d_ff_2_qn, d_ff_1_qn);
  D_Flip_Flop #(.Pre_Clr_Positions("LEGACY"), .NewFFLayout("false")) d_ff_4 (
    .clk(nand_2_out), .D(nand_3_out), .Q(d_ff_4_q), .reset(in_1));  // open: Qn, preset
  nand nand_4 (digital_oscilloscope_1_p4, d_ff_3_q, d_ff_4_q);
endmodule
