// Logisim project latches.circ as structural Verilog: 1 circuit, main circuit main
module main (
  input  S,
  input  S_2,
  input  R,
  input  R_2,
  input  S_3,
  input  R_3,
  output QNot,
  output QNot_2,
  output Q,
  output Q_2,
  output Q_3,
  output QNot_3
);

  nor nor_1 (QNot, S, Q);
  nor nor_2 (Q, QNot, R);
  nor nor_3 (QNot_3, S_3, Q_3);
  nor nor_4 (Q_3, QNot_3, R_3);
  nor nor_5 (QNot_2, S_2, Q_2);
  nor nor_6 (Q_2, QNot_2, R_2);
endmodule
