// Logisim project ram.circ as structural Verilog: 3 circuits, main circuit ram_1x1
// 1x1
module ram_1x1 (
  input  R_W,
  input  address,
  input  CLK,
  input  \input ,
  input  CLR,
  output \output 
);

  wire and_1_out, d_ff_1_q;

  and and_1 (and_1_out, address, R_W, CLK);
  D_Flip_Flop #(.Pre_Clr_Positions("LEGACY"), .NewFFLayout("false")) d_ff_1 (
    .clk(and_1_out), .D(\input ), .Q(d_ff_1_q), .reset(CLR));  // open: Qn, preset
  and and_2 (\output , address, d_ff_1_q);

  // Notes on the sheet:
  //   RAM 1x1
endmodule

module ram_1x2 (
  input  R_W,
  input  address,
  input  CLK,
  input  CLR,
  input  in0,
  input  in1,
  output out0,
  output out1
);

  ram_1x1 ram_1x1_1 (.R_W(R_W), .CLK(CLK), .CLR(CLR), .address(address), .\output (out1), .\input (in1));
  ram_1x1 ram_1x1_2 (.R_W(R_W), .CLK(CLK), .CLR(CLR), .address(address), .\output (out0), .\input (in0));
endmodule

module ram_2x1 (
  input  R_W,
  input  CLK,
  input  address,
  input  CLR,
  input  in,
  output out
);

  wire _0_output, _1_output, demultiplexer_1_out0, demultiplexer_1_out1;

  ram_1x1 _0 (.R_W(R_W), .CLK(CLK), .CLR(CLR), .address(demultiplexer_1_out0), .\output (_0_output), .\input (in));
  ram_1x1 _1 (.R_W(R_W), .CLK(CLK), .CLR(CLR), .address(demultiplexer_1_out1), .\output (_1_output), .\input (in));
  Demultiplexer #(.enable("false")) demultiplexer_1 (
    .out0(demultiplexer_1_out0), .out1(demultiplexer_1_out1), .in(1'b1), .sel(address));
  Multiplexer #(.enable("false")) multiplexer_1 (.in0(_0_output), .in1(_1_output), .out(out), .sel(address));
endmodule
