// Logisim project ring.circ as structural Verilog: 1 circuit, main circuit ring
module ring (
  input  in_1,
  input  in_2,
  output out_3
);

  wire button_1_out, clock_1_out, d_ff_1_q, d_ff_2_q, d_ff_3_q, or_1_out;

  Button button_1 (.out(button_1_out));
  or or_1 (or_1_out, button_1_out, clock_1_out);
  Clock clock_1 (.out(clock_1_out));
  // Probe on out_3
  D_Flip_Flop #(.Pre_Clr_Positions("LEGACY"), .NewFFLayout("false")) d_ff_1 (
    .clk(or_1_out), .D(out_3), .Q(d_ff_1_q), .preset(in_2), .reset(in_1));  // open: Qn
  // Probe on d_ff_3_q
  D_Flip_Flop #(.Pre_Clr_Positions("LEGACY"), .NewFFLayout("false")) d_ff_2 (
    .clk(or_1_out), .D(d_ff_1_q), .Q(d_ff_2_q), .reset(in_1));  // open: Qn, preset
  // Probe on d_ff_2_q
  D_Flip_Flop #(.Pre_Clr_Positions("LEGACY"), .NewFFLayout("false")) d_ff_3 (
    .clk(or_1_out), .D(d_ff_2_q), .Q(d_ff_3_q), .reset(in_1));  // open: Qn, preset
  // Probe on d_ff_1_q
  D_Flip_Flop #(.Pre_Clr_Positions("LEGACY"), .NewFFLayout("false")) d_ff_4 (
    .clk(or_1_out), .D(d_ff_3_q), .Q(out_3), .reset(in_1));  // open: Qn, preset
endmodule
