// Logisim project sap.circ as structural Verilog: 3 circuits, main circuit sap
module sap (
  output [3:0] High,
  output [3:0] Low
);

  wire [3:0] MAR_q;
  wire [7:0] MDR_q, Mem_data;

  Register #(.width(4), .Select("low")) MAR (.D(Low), .Q(MAR_q));  // open: en, clk, clr
  Controlled_Buffer #(.width(8)) controlled_buffer_1 (.in(MDR_q));  // open: out, en
  Register #(.Select("low")) MDR (.D(Mem_data), .Q(MDR_q));  // open: en, clk, clr
  RAM #(.addrWidth(4), .simpleMode("false"), .Select("low")) Mem (
    .addr(MAR_q), .data(Mem_data));  // open: sel, clk, ld, clr
  // Probe on High
  // Probe on Low
  Register #(.Select("low")) Output ();  // open: D, en, Q, clk, clr
  Hex_Digit_Display hex_digit_display_1 ();  // open: value, dp

  // Notes on the sheet:
  //   DBus
  //   ABus
endmodule

module decoder (
  input  in_1,
  input  in_2,
  input  in_3,
  input  in_4,
  output LDA,
  output ADD,
  output SUB,
  output OUT,
  output HLT
);

  wire and_1_out, not_1_out, not_2_out, not_3_out, not_4_out;

  not not_1 (not_1_out, in_1);
  not not_2 (not_2_out, in_4);
  not not_3 (not_3_out, in_3);
  not not_4 (not_4_out, in_2);
  and and_1 (and_1_out, not_2_out, not_3_out, not_4_out, not_1_out);
  // Probe on and_1_out
  and and_2 (LDA, in_4, not_3_out, not_4_out, not_1_out);
  and and_3 (ADD, not_2_out, in_3, not_4_out, not_1_out);
  and and_4 (SUB, in_4, in_3, not_4_out, not_1_out);
  and and_5 (OUT, not_2_out, in_3, in_2, in_1);
  and and_6 (HLT, in_4, in_3, in_2, in_1);
endmodule

module control_sequencer (
  input  CLK,
  input  CLR
);

  wire nor_1_out, not_1_out, shift_register_1_q0, shift_register_1_q1, shift_register_1_q2,
       shift_register_1_q3, shift_register_1_q4, shift_register_1_q5;

  Shift_Register #(.length(6)) shift_register_1 (
    .in(nor_1_out), .clk(not_1_out), .clr(CLR), .q0(shift_register_1_q0), .q1(shift_register_1_q1),
    .q2(shift_register_1_q2), .q3(shift_register_1_q3), .q4(shift_register_1_q4), .q5(shift_register_1_q5));  // open: shift, out, load, d0, d1, d2, d3, d4, d5
  not not_1 (not_1_out, CLK);
  nor nor_1 (nor_1_out, shift_register_1_q0, shift_register_1_q1, shift_register_1_q2, shift_register_1_q3, shift_register_1_q4);
endmodule
