// Logisim project subtractive-circuits.circ as structural Verilog: 4 circuits, main circuit half-subtractor
module half_subtractor (
  input  a,
  input  b,
  output s0,
  output s1
);

  wire not_1_out;

  not not_1 (not_1_out, a);
  xor xor_1 (s0, a, b);
  and and_1 (s1, not_1_out, b);
endmodule

module full_subtractor (
  input  a,
  input  b,
  input  borrow_in,
  output out_4,
  output out_5
);

  wire half_subtractor_1_s0, half_subtractor_1_s1, half_subtractor_2_s1;

  half_subtractor half_subtractor_1 (.a(a), .b(b), .s0(half_subtractor_1_s0), .s1(half_subtractor_1_s1));
  half_subtractor half_subtractor_2 (.a(half_subtractor_1_s0), .b(borrow_in), .s0(out_4), .s1(half_subtractor_2_s1));
  or or_1 (out_5, half_subtractor_2_s1, half_subtractor_1_s1);
endmodule

module byte_subtractor (
  input  [7:0] in_1,
  input  [7:0] in_2,
  output [7:0] out_3
);

  wire full_subtractor_1_out_5, full_subtractor_2_out_5, full_subtractor_3_out_5, full_subtractor_4_out_5,
       full_subtractor_5_out_5, full_subtractor_6_out_5, full_subtractor_7_out_5;

  full_subtractor full_subtractor_1 (
    .a(in_1[0]), .b(in_2[0]), .borrow_in(1'b0), .out_4(out_3[0]), .out_5(full_subtractor_1_out_5));
  full_subtractor full_subtractor_2 (
    .a(in_1[1]), .b(in_2[1]), .borrow_in(full_subtractor_1_out_5), .out_4(out_3[1]),
    .out_5(full_subtractor_2_out_5));
  full_subtractor full_subtractor_3 (
    .a(in_1[2]), .b(in_2[2]), .borrow_in(full_subtractor_2_out_5), .out_4(out_3[2]),
    .out_5(full_subtractor_3_out_5));
  full_subtractor full_subtractor_4 (
    .a(in_1[3]), .b(in_2[3]), .borrow_in(full_subtractor_3_out_5), .out_4(out_3[3]),
    .out_5(full_subtractor_4_out_5));
  full_subtractor full_subtractor_5 (
    .a(in_1[4]), .b(in_2[4]), .borrow_in(full_subtractor_4_out_5), .out_4(out_3[4]),
    .out_5(full_subtractor_5_out_5));
  full_subtractor full_subtractor_6 (
    .a(in_1[5]), .b(in_2[5]), .borrow_in(full_subtractor_5_out_5), .out_4(out_3[5]),
    .out_5(full_subtractor_6_out_5));
  full_subtractor full_subtractor_7 (
    .a(in_1[6]), .b(in_2[6]), .borrow_in(full_subtractor_6_out_5), .out_4(out_3[6]),
    .out_5(full_subtractor_7_out_5));
  full_subtractor full_subtractor_8 (
    .a(in_1[7]), .b(in_2[7]), .borrow_in(full_subtractor_7_out_5), .out_4(out_3[7]));  // open: out_5
endmodule

module complete_subtractor (
  input  [7:0] in_1,
  input  [7:0] in_2,
  output [7:0] out_3
);

  wire and_1_out, and_2_out, and_3_out, and_4_out, and_5_out, and_6_out, and_7_out, and_8_out, and_9_out,
       and_10_out, and_11_out, and_12_out, and_13_out, and_14_out, and_15_out, and_16_out, not_1_out,
       not_2_out, not_3_out, not_4_out, not_5_out, not_6_out, not_7_out, not_8_out, not_9_out, not_10_out,
       not_11_out, not_12_out, not_13_out, not_14_out, not_15_out, not_16_out, or_1_out, or_2_out, or_3_out,
       or_4_out, or_5_out, or_6_out, or_7_out, xor_1_out, xor_2_out, xor_3_out, xor_4_out, xor_5_out,
       xor_6_out, xor_7_out, xor_8_out;

  not not_1 (not_1_out, in_1[0]);
  not not_2 (not_2_out, in_1[1]);
  not not_3 (not_3_out, in_1[2]);
  not not_4 (not_4_out, in_1[3]);
  not not_5 (not_5_out, in_1[4]);
  not not_6 (not_6_out, in_1[5]);
  not not_7 (not_7_out, in_1[6]);
  not not_8 (not_8_out, in_1[7]);
  xor xor_1 (xor_1_out, in_1[0], in_2[0]);
  and and_1 (and_1_out, in_2[0], not_1_out);
  not not_9 (not_9_out, xor_1_out);
  xor xor_2 (xor_2_out, in_1[1], in_2[1]);
  and and_2 (and_2_out, in_2[1], not_2_out);
  not not_10 (not_10_out, xor_2_out);
  xor xor_3 (xor_3_out, in_1[2], in_2[2]);
  and and_3 (and_3_out, in_2[2], not_3_out);
  not not_11 (not_11_out, xor_3_out);
  xor xor_4 (xor_4_out, in_1[3], in_2[3]);
  and and_4 (and_4_out, in_2[3], not_4_out);
  not not_12 (not_12_out, xor_4_out);
  xor xor_5 (xor_5_out, in_1[4], in_2[4]);
  and and_5 (and_5_out, in_2[4], not_5_out);
  not not_13 (not_13_out, xor_5_out);
  xor xor_6 (xor_6_out, in_1[5], in_2[5]);
  and and_6 (and_6_out, in_2[5], not_6_out);
  xor xor_7 (xor_7_out, in_1[6], in_2[6]);
  and and_7 (and_7_out, in_2[6], not_7_out);
  xor xor_8 (xor_8_out, in_1[7], in_2[7]);
  and and_8 (and_8_out, in_2[7], not_8_out);
  xor xor_9 (out_3[0], xor_1_out, 1'b0);
  and and_9 (and_9_out, 1'b0, not_9_out);
  or or_1 (or_1_out, and_9_out, and_1_out);
  xor xor_10 (out_3[1], xor_2_out, or_1_out);
  and and_10 (and_10_out, or_1_out, not_10_out);
  or or_2 (or_2_out, and_10_out, and_2_out);
  xor xor_11 (out_3[2], xor_3_out, or_2_out);
  and and_11 (and_11_out, or_2_out, not_11_out);
  or or_3 (or_3_out, and_11_out, and_3_out);
  xor xor_12 (out_3[3], xor_4_out, or_3_out);
  and and_12 (and_12_out, or_3_out, not_12_out);
  or or_4 (or_4_out, and_12_out, and_4_out);
  xor xor_13 (out_3[4], xor_5_out, or_4_out);
  and and_13 (and_13_out, or_4_out, not_13_out);
  or or_5 (or_5_out, and_13_out, and_5_out);
  and and_14 (and_14_out, or_5_out, not_14_out);
  not not_14 (not_14_out, xor_6_out);
  and and_15 (and_15_out, or_6_out, not_15_out);
  not not_15 (not_15_out, xor_7_out);
  and and_16 (and_16_out, or_7_out, not_16_out);
  not not_16 (not_16_out, xor_8_out);
  xor xor_14 (out_3[5], xor_6_out, or_5_out);
  or or_6 (or_6_out, and_14_out, and_6_out);
  xor xor_15 (out_3[6], xor_7_out, or_6_out);
  or or_7 (or_7_out, and_15_out, and_7_out);
  xor xor_16 (out_3[7], xor_8_out, or_7_out);
  // OR_Gate or_8 has open pins: in0=and_16_out, in1=and_8_out, out=open
endmodule
